// Logisim project Adders.circ as structural Verilog
module Half_Adder (
  input  x,
  input  y,
  output Sum,
  output Carry
);

  xor xor_1 (Sum, x, y);
  and and_1 (Carry, y, x);
endmodule

module Full_Adder (
  input  x,
  input  y,
  input  Ci,
  output Sum,
  output Carry
);

  wire half_adder_1_carry, half_adder_1_sum, half_adder_2_carry;

  Half_Adder half_adder_1 (.Sum(half_adder_1_sum), .Carry(half_adder_1_carry), .x(x), .y(y));
  Half_Adder half_adder_2 (.Sum(Sum), .Carry(half_adder_2_carry), .x(half_adder_1_sum), .y(Ci));
  or or_1 (Carry, half_adder_2_carry, half_adder_1_carry);
endmodule

module Half_Subtractor (
  input  x,
  input  y,
  output Difference,
  output Borrow
);

  wire not_1_out;

  not not_1 (not_1_out, x);
  xor xor_1 (Difference, x, y);
  and and_1 (Borrow, y, not_1_out);
endmodule

module Full_Subtractor (
  input  x,
  input  y,
  input  z,
  output Difference,
  output Borrow
);

  wire half_subtractor_1_borrow, half_subtractor_1_difference, half_subtractor_2_borrow;

  Half_Subtractor half_subtractor_1 (
    .Difference(half_subtractor_1_difference), .Borrow(half_subtractor_1_borrow), .x(x), .y(y));
  Half_Subtractor half_subtractor_2 (
    .Difference(Difference), .Borrow(half_subtractor_2_borrow), .x(half_subtractor_1_difference), .y(z));
  or or_1 (Borrow, half_subtractor_2_borrow, half_subtractor_1_borrow);
endmodule

module _4_Bit_Parallel_Binary_Adder (
  input  B3,
  input  B2,
  input  B1,
  input  B0,
  input  A3,
  input  A2,
  input  A1,
  input  A0,
  input  Ci,
  output Co,
  output S3,
  output S2,
  output S1,
  output S0
);

  wire full_adder_2_carry, full_adder_3_carry, full_adder_4_carry;

  Full_Adder full_adder_1 (.Sum(S3), .Carry(Co), .x(A3), .y(B3), .Ci(full_adder_2_carry));
  Full_Adder full_adder_2 (.Sum(S2), .Carry(full_adder_2_carry), .x(A2), .y(B2), .Ci(full_adder_3_carry));
  Full_Adder full_adder_3 (.Sum(S1), .Carry(full_adder_3_carry), .x(A1), .y(B1), .Ci(full_adder_4_carry));
  Full_Adder full_adder_4 (.Sum(S0), .Carry(full_adder_4_carry), .x(A0), .y(B0), .Ci(Ci));
endmodule

module BCD_to_XS3_Converter (
  input  B3,
  input  B2,
  input  B1,
  input  B0,
  output i,
  output C3,
  output C2,
  output C1,
  output C0
);

  wire not_1_out;

  not not_1 (not_1_out, 1'b1);
  _4_Bit_Parallel_Binary_Adder u_4_bit_parallel_binary_adder_1 (
    .Ci(not_1_out), .B3(not_1_out), .B2(not_1_out), .B1(1'b1), .B0(1'b1), .A3(B3), .A2(B2), .A1(B1), .A0(B0),
    .Co(i), .S3(C3), .S2(C2), .S1(C1), .S0(C0));
endmodule

module _4_Bit_BCD_Adder (
  input  B3,
  input  B2,
  input  B1,
  input  B0,
  input  A3,
  input  A2,
  input  A1,
  input  A0,
  input  Ci0,
  output Co,
  output S3,
  output S2,
  output S1,
  output S0
);

  wire and_1_out, and_2_out, n4_bit_parallel_binary_adder_1_co, n4_bit_parallel_binary_adder_1_s0,
       n4_bit_parallel_binary_adder_1_s1, n4_bit_parallel_binary_adder_1_s2,
       n4_bit_parallel_binary_adder_1_s3, not_1_out;

  or or_1 (Co, n4_bit_parallel_binary_adder_1_co, and_1_out, and_2_out);
  and and_1 (and_1_out, n4_bit_parallel_binary_adder_1_s3, n4_bit_parallel_binary_adder_1_s2);
  and and_2 (and_2_out, n4_bit_parallel_binary_adder_1_s3, n4_bit_parallel_binary_adder_1_s1);
  not not_1 (not_1_out, 1'b1);
  _4_Bit_Parallel_Binary_Adder u_4_bit_parallel_binary_adder_1 (
    .Ci(Ci0), .B3(B3), .B2(B2), .B1(B1), .B0(B0), .A3(A3), .A2(A2), .A1(A1), .A0(A0),
    .Co(n4_bit_parallel_binary_adder_1_co), .S3(n4_bit_parallel_binary_adder_1_s3),
    .S2(n4_bit_parallel_binary_adder_1_s2), .S1(n4_bit_parallel_binary_adder_1_s1),
    .S0(n4_bit_parallel_binary_adder_1_s0));
  _4_Bit_Parallel_Binary_Adder u_4_bit_parallel_binary_adder_2 (
    .Ci(1'b0), .B3(not_1_out), .B2(Co), .B1(Co), .B0(not_1_out), .A3(n4_bit_parallel_binary_adder_1_s3),
    .A2(n4_bit_parallel_binary_adder_1_s2), .A1(n4_bit_parallel_binary_adder_1_s1),
    .A0(n4_bit_parallel_binary_adder_1_s0), .S3(S3), .S2(S2), .S1(S1), .S0(S0));  // open: Co
endmodule

module _4_Bit_Magnitude_Comparator (
  input  B3,
  input  B2,
  input  B1,
  input  B0,
  input  A3,
  input  A2,
  input  A1,
  input  A0,
  output A_B,
  output A_B_2,
  output A__B
);

  wire and_1_out, and_2_out, and_3_out, and_4_out, and_5_out, and_6_out, and_8_out, and_9_out, xnor_1_out,
       xnor_2_out, xnor_3_out, xnor_4_out;

  xnor xnor_1 (xnor_1_out, B3, A3);
  and and_1 (and_1_out, ~B3, A3);  // AND_Gate
  and and_2 (and_2_out, B3, ~A3);  // AND_Gate
  xnor xnor_2 (xnor_2_out, B2, A2);
  and and_3 (and_3_out, ~B2, xnor_1_out, A2);  // AND_Gate
  and and_4 (and_4_out, B2, xnor_1_out, ~A2);  // AND_Gate
  or or_1 (A_B, and_2_out, and_4_out, and_6_out, and_9_out);
  xnor xnor_3 (xnor_3_out, B1, A1);
  and and_5 (and_5_out, ~B1, xnor_1_out, xnor_2_out, A1);  // AND_Gate
  or or_2 (A_B_2, and_1_out, and_3_out, and_5_out, and_8_out);
  and and_6 (and_6_out, B1, xnor_1_out, xnor_2_out, ~A1);  // AND_Gate
  and and_7 (A__B, xnor_1_out, xnor_2_out, xnor_3_out, xnor_4_out);
  xnor xnor_4 (xnor_4_out, B0, A0);
  and and_8 (and_8_out, ~B0, xnor_1_out, xnor_2_out, xnor_3_out, A0);  // AND_Gate
  and and_9 (and_9_out, B0, xnor_1_out, xnor_2_out, xnor_3_out, ~A0);  // AND_Gate
endmodule

module _4_Bit_Serial_Binary_Adder (
  input  B3,
  input  B2,
  input  B1,
  input  B0,
  input  A3,
  input  A2,
  input  A1,
  input  A0,
  input  Clk,
  input  Preset,
  input  En,
  input  Clear,
  input  [1:0] SelectLine,
  input  ExternalInput,
  output Co,
  output S3,
  output S2,
  output S1,
  output S0
);

  wire and_1_out, full_adder_1_carry, full_adder_1_sum,
       n4_bit_bidirectional_shift_register_with_parallel_load_2_out0__right_shift_output;

  _4_Bit_Bidirectional_Shift_Register_With_Parallel_Load u_4_bit_bidirectional_shift_register_with_parallel_load_1 (
    .Clk(Clk), .Pr(Preset), .En(En), .Clr(Clear), .Select_Line(SelectLine),
    .Right_Shift_Input(full_adder_1_sum), .Out3__Let_SHift_Output(S3), .Out2(S2), .Out1(S1),
    .Out0__Right_Shift_Output(S0), .Inp3(A3), .Inp2(A2), .Inp1(A1), .Inp0(A0));  // open: Left_Shift_Input
  _4_Bit_Bidirectional_Shift_Register_With_Parallel_Load u_4_bit_bidirectional_shift_register_with_parallel_load_2 (
    .Clk(Clk), .Pr(Preset), .En(En), .Clr(Clear), .Select_Line(SelectLine),
    .Right_Shift_Input(ExternalInput),
    .Out0__Right_Shift_Output(n4_bit_bidirectional_shift_register_with_parallel_load_2_out0__right_shift_output),
    .Inp3(B3), .Inp2(B2), .Inp1(B1), .Inp0(B0));  // open: Left_Shift_Input, Out3__Let_SHift_Output, Out2, Out1
  Full_Adder full_adder_1 (
    .Sum(full_adder_1_sum), .Carry(full_adder_1_carry), .x(S0),
    .y(n4_bit_bidirectional_shift_register_with_parallel_load_2_out0__right_shift_output), .Ci(Co));
  D_Flip_Flop d_ff_1 (
    .clk(and_1_out), .D(full_adder_1_carry), .Q(Co), .preset(Preset), .en(En), .reset(Clear));  // open: Qn
  and and_1 (and_1_out, SelectLine[1], Clk);
endmodule
