// Logisim project Basic_Flipflops.circ as structural Verilog
module RS_FF_NOR_LATCH (
  input  Reset,
  input  Set,
  output Out,
  output nOut
);

  nor nor_1 (Out, Reset, nOut);
  nor nor_2 (nOut, Out, Set);
endmodule

module Clocked_RS_FF_NOR_LATCh (
  input  Set,
  input  Clk,
  input  Reset,
  output Out,
  output nOut
);

  wire and_1_out, and_2_out;

  and and_1 (and_1_out, Reset, Clk);
  and and_2 (and_2_out, Clk, Set);
  nor nor_1 (Out, and_1_out, nOut);
  nor nor_2 (nOut, Out, and_2_out);
endmodule

module Master_Slave_RS_FF_NOR_LATCh (
  input  Set,
  input  nClk,
  input  Reset,
  output Out,
  output nout
);

  wire clocked_rs_ff_nor_latch_1_nout, clocked_rs_ff_nor_latch_1_out, not_1_out;

  Clocked_RS_FF_NOR_LATCh clocked_rs_ff_nor_latch_1 (
    .Reset(Set), .Clk(nClk), .Set(Reset), .Out(clocked_rs_ff_nor_latch_1_out),
    .nOut(clocked_rs_ff_nor_latch_1_nout));
  Clocked_RS_FF_NOR_LATCh clocked_rs_ff_nor_latch_2 (
    .Reset(clocked_rs_ff_nor_latch_1_out), .Clk(not_1_out), .Set(clocked_rs_ff_nor_latch_1_nout), .Out(Out),
    .nOut(nout));
  not not_1 (not_1_out, nClk);
endmodule

module Master_Slave_JK_FF (
  input  J,
  input  nClk,
  input  K,
  input  in_4,
  input  in_5,
  input  in_6,
  output Out,
  output nOut
);

  wire j_k_ff_1_q, j_k_ff_1_qn, not_1_out;

  J_K_Flip_Flop j_k_ff_1 (
    .J(J), .clk(nClk), .K(K), .Q(j_k_ff_1_q), .Qn(j_k_ff_1_qn), .preset(in_4), .en(in_5), .reset(in_6));
  not not_1 (not_1_out, nClk);
  J_K_Flip_Flop j_k_ff_2 (
    .J(j_k_ff_1_q), .clk(not_1_out), .K(j_k_ff_1_qn), .Q(Out), .Qn(nOut));  // open: preset, en, reset
endmodule

module Clocked_D_FF_NAND_LATCH (
  input  D,
  input  Clk,
  output Out,
  output nOut
);

  wire nand_1_out, nand_2_out, not_1_out;

  not not_1 (not_1_out, D);
  nand nand_1 (nand_1_out, D, Clk);
  nand nand_2 (nand_2_out, Clk, not_1_out);
  nand nand_3 (Out, nand_1_out, nOut);
  nand nand_4 (nOut, Out, nand_2_out);
endmodule

module Edge_Triggered_D_FF_NAND_Latch (
  input  Clk,
  input  D,
  output Q,
  output nQ
);

  wire _1_out, _2_out, _3_out, _4_out;

  nand _1 (_1_out, _4_out, _2_out);
  nand _2 (_2_out, _1_out, Clk);
  nand _3 (_3_out, _2_out, Clk, _4_out);
  nand _4 (_4_out, _3_out, D);
  nand _5 (Q, _2_out, nQ);
  nand _6 (nQ, Q, _3_out);

  // Notes on the sheet:
  //   FF1
  //   FF2
  //   Set
  //   Reset
  //   FF3
endmodule
