// Logisim project Counters.circ as structural Verilog
module _4_Bit_Binary_Synchronous_Up_Counter_JK_FF (
  input  Clk,
  input  CountEn,
  input  Preset,
  input  En,
  input  Clear,
  output Next,
  output A3,
  output A2,
  output A1,
  output A0
);

  wire and_1_out, and_2_out, and_3_out;

  J_K_Flip_Flop j_k_ff_1 (
    .J(CountEn), .clk(Clk), .K(CountEn), .Q(A0), .preset(Preset), .en(En), .reset(Clear));  // open: Qn
  and and_1 (and_1_out, CountEn, A0);
  J_K_Flip_Flop j_k_ff_2 (
    .J(and_1_out), .clk(Clk), .K(and_1_out), .Q(A1), .preset(Preset), .en(En), .reset(Clear));  // open: Qn
  and and_2 (and_2_out, and_1_out, A1);
  and and_3 (and_3_out, and_2_out, A2);
  J_K_Flip_Flop j_k_ff_3 (
    .J(and_2_out), .clk(Clk), .K(and_2_out), .Q(A2), .preset(Preset), .en(En), .reset(Clear));  // open: Qn
  J_K_Flip_Flop j_k_ff_4 (
    .J(and_3_out), .clk(Clk), .K(and_3_out), .Q(A3), .preset(Preset), .en(En), .reset(Clear));  // open: Qn
  and and_4 (Next, and_3_out, A3);
endmodule

module _4_Bit_Binary_Synchronous_Down_Counter_JK_FF (
  input  Clk,
  input  CountEn,
  input  Preset,
  input  En,
  input  Clear,
  output Next,
  output A3,
  output A2,
  output A1,
  output A0
);

  wire and_1_out, and_2_out, and_3_out, j_k_ff_1_q, j_k_ff_2_q, j_k_ff_3_q, j_k_ff_4_q;

  J_K_Flip_Flop j_k_ff_1 (
    .J(CountEn), .clk(Clk), .K(CountEn), .Q(j_k_ff_1_q), .Qn(A0), .preset(Preset), .en(En), .reset(Clear));
  and and_1 (and_1_out, CountEn, j_k_ff_1_q);
  and and_2 (and_2_out, and_1_out, j_k_ff_2_q);
  J_K_Flip_Flop j_k_ff_2 (
    .J(and_1_out), .clk(Clk), .K(and_1_out), .Q(j_k_ff_2_q), .Qn(A1), .preset(Preset), .en(En), .reset(Clear));
  J_K_Flip_Flop j_k_ff_3 (
    .J(and_2_out), .clk(Clk), .K(and_2_out), .Q(j_k_ff_3_q), .Qn(A2), .preset(Preset), .en(En), .reset(Clear));
  and and_3 (and_3_out, and_2_out, j_k_ff_3_q);
  and and_4 (Next, and_3_out, j_k_ff_4_q);
  J_K_Flip_Flop j_k_ff_4 (
    .J(and_3_out), .clk(Clk), .K(and_3_out), .Q(j_k_ff_4_q), .Qn(A3), .preset(Preset), .en(En), .reset(Clear));
endmodule

module _4_Bit_Binary_Synchronous_Up_Down_Counter_T_FF (
  input  UpEn,
  input  DownEn,
  input  Clk,
  input  Preset,
  input  En,
  input  Clear,
  output DownNext,
  output UpNext,
  output A3,
  output A2,
  output A1,
  output A0
);

  wire and_1_out, and_2_out, and_3_out, and_4_out, and_5_out, and_6_out, or_1_out, or_2_out, or_3_out,
       or_4_out, t_ff_1_qn, t_ff_2_qn, t_ff_3_qn, t_ff_4_qn;

  or or_1 (or_1_out, DownEn, UpEn);
  T_Flip_Flop t_ff_1 (.clk(Clk), .T(or_1_out), .Q(A0), .Qn(t_ff_1_qn), .preset(Preset), .reset(Clear), .en(En));
  and and_1 (and_1_out, UpEn, A0);
  and and_2 (and_2_out, DownEn, t_ff_1_qn);
  or or_2 (or_2_out, and_2_out, and_1_out);
  T_Flip_Flop t_ff_2 (.clk(Clk), .T(or_2_out), .Q(A1), .Qn(t_ff_2_qn), .preset(Preset), .reset(Clear), .en(En));
  and and_3 (and_3_out, and_1_out, A1);
  and and_4 (and_4_out, and_2_out, t_ff_2_qn);
  or or_3 (or_3_out, and_4_out, and_3_out);
  T_Flip_Flop t_ff_3 (.clk(Clk), .T(or_3_out), .Q(A2), .Qn(t_ff_3_qn), .preset(Preset), .reset(Clear), .en(En));
  and and_5 (and_5_out, and_3_out, A2);
  and and_6 (and_6_out, and_4_out, t_ff_3_qn);
  or or_4 (or_4_out, and_6_out, and_5_out);
  T_Flip_Flop t_ff_4 (.clk(Clk), .T(or_4_out), .Q(A3), .Qn(t_ff_4_qn), .preset(Preset), .reset(Clear), .en(En));
  and and_7 (DownNext, and_5_out, A3);
  and and_8 (UpNext, and_6_out, t_ff_4_qn);
endmodule

module _4_Bir_Binary_Synchronous_Up_Down_Counter_With_Parallel_Load_T_FF (
  input  L2,
  input  L1,
  input  L3,
  input  L0,
  input  Load,
  input  DownEn,
  input  UpEn,
  input  Clk,
  input  Preset,
  input  En,
  input  Clear,
  output DownNext,
  output UpNext,
  output A3,
  output A2,
  output A1,
  output A0
);

  wire and_1_out, and_2_out, and_3_out, and_4_out, and_5_out, and_6_out, and_7_out, and_8_out, and_9_out,
       and_10_out, or_1_out, or_2_out, or_3_out, or_4_out, or_5_out, or_6_out, or_7_out, or_8_out, t_ff_1_qn,
       t_ff_2_qn, t_ff_3_qn, t_ff_4_qn;

  and and_1 (and_1_out, Load, L0);
  or or_1 (or_1_out, UpEn, DownEn);
  or or_2 (or_2_out, and_1_out, Preset);
  T_Flip_Flop t_ff_1 (.clk(Clk), .T(or_1_out), .Q(A0), .Qn(t_ff_1_qn), .preset(or_2_out), .reset(Clear), .en(En));
  and and_2 (and_2_out, Load, L1);
  and and_3 (and_3_out, DownEn, A0);
  and and_4 (and_4_out, UpEn, t_ff_1_qn);
  or or_3 (or_3_out, and_4_out, and_3_out);
  T_Flip_Flop t_ff_2 (.clk(Clk), .T(or_3_out), .Q(A1), .Qn(t_ff_2_qn), .preset(or_4_out), .reset(Clear), .en(En));
  or or_4 (or_4_out, and_2_out, Preset);
  and and_5 (and_5_out, and_3_out, A1);
  and and_6 (and_6_out, and_4_out, t_ff_2_qn);
  and and_7 (and_7_out, Load, L2);
  or or_5 (or_5_out, and_6_out, and_5_out);
  T_Flip_Flop t_ff_3 (.clk(Clk), .T(or_5_out), .Q(A2), .Qn(t_ff_3_qn), .preset(or_6_out), .reset(Clear), .en(En));
  or or_6 (or_6_out, and_7_out, Preset);
  and and_8 (and_8_out, Load, L3);
  and and_9 (and_9_out, and_5_out, A2);
  and and_10 (and_10_out, and_6_out, t_ff_3_qn);
  or or_7 (or_7_out, and_10_out, and_9_out);
  T_Flip_Flop t_ff_4 (.clk(Clk), .T(or_7_out), .Q(A3), .Qn(t_ff_4_qn), .preset(or_8_out), .reset(Clear), .en(En));
  or or_8 (or_8_out, and_8_out, Preset);
  and and_11 (DownNext, and_9_out, A3);
  and and_12 (UpNext, and_10_out, t_ff_4_qn);
endmodule

module _4_Bit_Ring_Counter_D_FF (
  input  Clk,
  input  En,
  input  Preset,
  input  Init,
  input  Clear,
  output A0,
  output A1,
  output A2,
  output A3
);

  wire or_1_out, or_2_out, or_3_out, or_4_out;

  D_Flip_Flop d_ff_1 (.clk(Clk), .D(A3), .Q(A0), .preset(or_1_out), .en(En), .reset(Clear));  // open: Qn
  or or_1 (or_1_out, Preset, Init);
  or or_2 (or_2_out, Clear, Init);
  D_Flip_Flop d_ff_2 (.clk(Clk), .D(A0), .Q(A1), .preset(Preset), .en(En), .reset(or_2_out));  // open: Qn
  D_Flip_Flop d_ff_3 (.clk(Clk), .D(A1), .Q(A2), .preset(Preset), .en(En), .reset(or_3_out));  // open: Qn
  or or_3 (or_3_out, Clear, Init);
  D_Flip_Flop d_ff_4 (.clk(Clk), .D(A2), .Q(A3), .preset(Preset), .en(En), .reset(or_4_out));  // open: Qn
  or or_4 (or_4_out, Clear, Init);
endmodule

module _4_Bit_Johnson_Counter_D_FF (
  input  Clk,
  input  En,
  input  Preset,
  input  Init,
  input  Clear,
  output A0,
  output A1,
  output A2,
  output A3
);

  wire d_ff_4_qn, or_1_out, or_2_out, or_3_out, or_4_out;

  D_Flip_Flop d_ff_1 (.clk(Clk), .D(d_ff_4_qn), .Q(A0), .preset(or_1_out), .en(En), .reset(Clear));  // open: Qn
  or or_1 (or_1_out, Preset, Init);
  or or_2 (or_2_out, Clear, Init);
  D_Flip_Flop d_ff_2 (.clk(Clk), .D(A0), .Q(A1), .preset(Preset), .en(En), .reset(or_2_out));  // open: Qn
  D_Flip_Flop d_ff_3 (.clk(Clk), .D(A1), .Q(A2), .preset(Preset), .en(En), .reset(or_3_out));  // open: Qn
  or or_3 (or_3_out, Clear, Init);
  D_Flip_Flop d_ff_4 (.clk(Clk), .D(A2), .Q(A3), .Qn(d_ff_4_qn), .preset(Preset), .en(En), .reset(or_4_out));
  or or_4 (or_4_out, Clear, Init);
endmodule

module _4_Bit_Binary_Asynchronous_Up_Counter_JK_FF (
  input  nClk,
  input  Preset,
  input  En,
  input  Clear,
  output A3,
  output A2,
  output A1,
  output A0
);

  J_K_Flip_Flop #(.trigger("falling")) j_k_ff_1 (
    .J(1'b1), .clk(nClk), .K(1'b1), .Q(A0), .preset(Preset), .en(En), .reset(Clear));  // open: Qn
  J_K_Flip_Flop #(.trigger("falling")) j_k_ff_2 (
    .J(1'b1), .clk(A0), .K(1'b1), .Q(A1), .preset(Preset), .en(En), .reset(Clear));  // open: Qn
  J_K_Flip_Flop #(.trigger("falling")) j_k_ff_3 (
    .J(1'b1), .clk(A1), .K(1'b1), .Q(A2), .preset(Preset), .en(En), .reset(Clear));  // open: Qn
  J_K_Flip_Flop #(.trigger("falling")) j_k_ff_4 (
    .J(1'b1), .clk(A2), .K(1'b1), .Q(A3), .preset(Preset), .en(En), .reset(Clear));  // open: Qn
endmodule

module _4_Bit_Binary_Asynchronous_Down_Counter_JK_FF (
  input  nClk,
  input  Preset,
  input  En,
  input  Clear,
  output A3,
  output A2,
  output A1,
  output A0
);

  wire j_k_ff_1_q, j_k_ff_2_q, j_k_ff_3_q;

  J_K_Flip_Flop #(.trigger("falling")) j_k_ff_1 (
    .J(1'b1), .clk(nClk), .K(1'b1), .Q(j_k_ff_1_q), .Qn(A0), .preset(Preset), .en(En), .reset(Clear));
  J_K_Flip_Flop #(.trigger("falling")) j_k_ff_2 (
    .J(1'b1), .clk(j_k_ff_1_q), .K(1'b1), .Q(j_k_ff_2_q), .Qn(A1), .preset(Preset), .en(En), .reset(Clear));
  J_K_Flip_Flop #(.trigger("falling")) j_k_ff_3 (
    .J(1'b1), .clk(j_k_ff_2_q), .K(1'b1), .Q(j_k_ff_3_q), .Qn(A2), .preset(Preset), .en(En), .reset(Clear));
  J_K_Flip_Flop #(.trigger("falling")) j_k_ff_4 (
    .J(1'b1), .clk(j_k_ff_3_q), .K(1'b1), .Qn(A3), .preset(Preset), .en(En), .reset(Clear));  // open: Q
endmodule
