// Logisim project Encoders_And_Decoders.circ as structural Verilog
module _3_8_Line_Decoder_Demutiplexer (
  input  En,
  input  B2,
  input  B1,
  input  B0,
  output D0,
  output D1,
  output D2,
  output D3,
  output D4,
  output D5,
  output D6,
  output D7
);

  wire not_1_out, not_2_out, not_3_out;

  not not_1 (not_1_out, B2);
  not not_2 (not_2_out, B1);
  not not_3 (not_3_out, B0);
  and and_1 (D0, En, not_1_out, not_2_out, not_3_out);
  and and_2 (D1, En, not_1_out, not_2_out, B0);
  and and_3 (D2, En, not_1_out, B1, not_3_out);
  and and_4 (D3, En, not_1_out, B1, B0);
  and and_5 (D4, En, B2, not_2_out, not_3_out);
  and and_6 (D5, En, B2, not_2_out, B0);
  and and_7 (D6, En, B2, B1, not_3_out);
  and and_8 (D7, En, B2, B1, B0);
endmodule

module Octal_to_Binary_Encoder (
  input  D0,
  input  D1,
  input  D2,
  input  D3,
  input  D4,
  input  D5,
  input  D6,
  input  D7,
  output B2,
  output B1,
  output B0
);

  or or_1 (B2, D4, D5, D6, D7);
  or or_2 (B1, D2, D3, D6, D7);
  or or_3 (B0, D1, D3, D5, D7);
endmodule

module _4_1_MUltiplexer (
  input  Input0,
  input  Input1,
  input  Input2,
  input  Input3,
  input  En,
  input  S1,
  input  S0,
  output Output
);

  wire and_1_out, and_2_out, and_3_out, and_4_out, not_1_out, not_2_out, or_1_out;

  not not_1 (not_1_out, S1);
  not not_2 (not_2_out, S0);
  and and_1 (and_1_out, Input0, not_1_out, not_2_out);
  and and_2 (and_2_out, Input1, not_1_out, S0);
  and and_3 (and_3_out, Input2, S1, not_2_out);
  and and_4 (and_4_out, Input3, S1, S0);
  or or_1 (or_1_out, and_1_out, and_2_out, and_3_out, and_4_out);
  and and_5 (Output, or_1_out, En);
endmodule

module _8_3_Line_Priority_Encoder (
  input  D0,
  input  D1,
  input  D2,
  input  D3,
  input  D4,
  input  D5,
  input  D6,
  input  D7,
  output B2,
  output B1,
  output B0
);

  wire and_1_out, and_2_out, and_3_out, and_4_out, or_1_out, or_2_out;

  or or_1 (or_1_out, D2, D3);
  and and_1 (and_1_out, D3, ~D4);  // AND_Gate
  and and_2 (and_2_out, D1, ~D2, ~D4);  // AND_Gate
  and and_3 (and_3_out, ~D4, or_1_out, ~D5);  // AND_Gate
  or or_2 (or_2_out, and_1_out, and_2_out, D5);
  or or_3 (B2, D4, D5, D7, D6);
  or or_4 (B1, D7, D6, and_3_out);
  and and_4 (and_4_out, or_2_out, ~D6);  // AND_Gate
  or or_5 (B0, and_4_out, D7);
endmodule
