// Logisim project ErrorDetectionCodes.circ as structural Verilog
module Parity_Bit_Generator_For_3_Bit_Data (
  input  D2,
  input  D1,
  input  D0,
  output Odd_Parity,
  output Even_Parity,
  output B2,
  output B1,
  output B0
);

  wire xor_1_out;

  not not_1 (Odd_Parity, Even_Parity);
  xor xor_1 (xor_1_out, D2, D1);
  xor xor_2 (Even_Parity, xor_1_out, D0);

  assign B0 = D0;
  assign B1 = D1;
  assign B2 = D2;
endmodule

module Block_Parity_Generator_For_3x3_Bit_Data_Block (
  input  [2:0] DataSet0,
  input  [2:0] DataSet1,
  input  [2:0] DataSet2,
  output [4:0] out_4,
  output [4:0] out_5,
  output [4:0] out_6,
  output [2:0] Even_Parity_for_Data_Column,
  output [2:0] Odd_Parity_for_Data_Column
);

  Parity_Bit_Generator_For_3_Bit_Data parity_bit_generator_for_3_bit_data_1 (
    .D2(DataSet0[2]), .D1(DataSet0[1]), .D0(DataSet0[0]), .Odd_Parity(out_4[4]), .Even_Parity(out_4[3]),
    .B2(out_4[2]), .B1(out_4[1]), .B0(out_4[0]));
  Parity_Bit_Generator_For_3_Bit_Data parity_bit_generator_for_3_bit_data_2 (
    .D2(DataSet1[2]), .D1(DataSet1[1]), .D0(DataSet1[0]), .Odd_Parity(out_5[4]), .Even_Parity(out_5[3]),
    .B2(out_5[2]), .B1(out_5[1]), .B0(out_5[0]));
  Parity_Bit_Generator_For_3_Bit_Data parity_bit_generator_for_3_bit_data_3 (
    .D2(DataSet2[2]), .D1(DataSet2[1]), .D0(DataSet2[0]), .Odd_Parity(out_6[4]), .Even_Parity(out_6[3]),
    .B2(out_6[2]), .B1(out_6[1]), .B0(out_6[0]));
  Parity_Bit_Generator_For_3_Bit_Data parity_bit_generator_for_3_bit_data_4 (
    .D2(DataSet2[0]), .D1(DataSet1[0]), .D0(DataSet0[0]), .Odd_Parity(Odd_Parity_for_Data_Column[0]),
    .Even_Parity(Even_Parity_for_Data_Column[0]));  // open: B2, B1, B0
  Parity_Bit_Generator_For_3_Bit_Data parity_bit_generator_for_3_bit_data_5 (
    .D2(DataSet2[1]), .D1(DataSet1[1]), .D0(DataSet0[1]), .Odd_Parity(Odd_Parity_for_Data_Column[1]),
    .Even_Parity(Even_Parity_for_Data_Column[1]));  // open: B2, B1, B0
  Parity_Bit_Generator_For_3_Bit_Data parity_bit_generator_for_3_bit_data_6 (
    .D2(DataSet2[2]), .D1(DataSet1[2]), .D0(DataSet0[2]), .Odd_Parity(Odd_Parity_for_Data_Column[2]),
    .Even_Parity(Even_Parity_for_Data_Column[2]));  // open: B2, B1, B0
endmodule

module Bi_quinary_Code_Generator (
  input  D3,
  input  D2,
  input  D1,
  input  D0,
  output _5W,
  output _0W,
  output _4W,
  output _3W,
  output _2W,
  output _1W,
  output _0W_2
);

  wire and_1_out, and_2_out, and_3_out, and_4_out, and_5_out, and_6_out, and_7_out, and_8_out, and_9_out,
       and_10_out;

  and and_1 (and_1_out, ~D0, ~D1, ~D2, ~D3);  // AND_Gate
  and and_2 (and_2_out, D0, ~D1, D2, ~D3);  // AND_Gate
  and and_3 (and_3_out, D0, ~D1, ~D2, ~D3);  // AND_Gate
  and and_4 (and_4_out, ~D0, D1, D2, ~D3);  // AND_Gate
  and and_5 (and_5_out, ~D0, D1, ~D2, ~D3);  // AND_Gate
  and and_6 (and_6_out, D0, D1, D2, ~D3);  // AND_Gate
  and and_7 (and_7_out, D0, D1, ~D2, ~D3);  // AND_Gate
  and and_8 (and_8_out, ~D0, ~D1, ~D2, D3);  // AND_Gate
  and and_9 (and_9_out, ~D0, ~D1, D2, ~D3);  // AND_Gate
  and and_10 (and_10_out, D0, ~D1, ~D2, D3);  // AND_Gate
  or or_1 (_5W, and_10_out, and_8_out, and_6_out, and_4_out, and_2_out);
  or or_2 (_0W, and_9_out, and_7_out, and_5_out, and_3_out, and_1_out);
  or or_3 (_0W_2, and_1_out, and_2_out);
  or or_4 (_1W, and_3_out, and_4_out);
  or or_5 (_2W, and_5_out, and_6_out);
  or or_6 (_3W, and_7_out, and_8_out);
  or or_7 (_4W, and_9_out, and_10_out);
endmodule

module Hamming_Code_Generator_For_4_Bit_Data (
  input  B3,
  input  B2,
  input  B1,
  input  B0,
  output B3_2,
  output B2_2,
  output B1_2,
  output P2,
  output B0_2,
  output P1,
  output P0
);

  Parity_Bit_Generator_For_3_Bit_Data parity_bit_generator_for_3_bit_data_1 (
    .D2(B3), .D1(B1), .D0(B0), .Odd_Parity(P0));  // open: Even_Parity, B2, B1, B0
  Parity_Bit_Generator_For_3_Bit_Data parity_bit_generator_for_3_bit_data_2 (
    .D2(B3), .D1(B2), .D0(B0), .Odd_Parity(P1));  // open: Even_Parity, B2, B1, B0
  Parity_Bit_Generator_For_3_Bit_Data parity_bit_generator_for_3_bit_data_3 (
    .D2(B3), .D1(B2), .D0(B1), .Odd_Parity(P2));  // open: Even_Parity, B2, B1, B0

  assign B0_2 = B0;
  assign B1_2 = B1;
  assign B2_2 = B2;
  assign B3_2 = B3;
endmodule
