// Logisim project Gates(CMOS).circ as structural Verilog
module NOT_Gate_Inverter (
  input  INP,
  output nINP
);

  Transistor transistor_1 (.in(1'b1), .out(nINP), .gate(INP));
  Transistor #(.\type ("n")) transistor_2 (.in(1'b0), .out(nINP), .gate(INP));

  // Notes on the sheet:
  //   S
  //   G
  //   D
  //   P
  //   G
  //   N
  //   D
  //   S
endmodule

module BUFFER (
  input  INP,
  output nINP,
  output INP_2
);

  Transistor transistor_1 (.in(1'b1), .out(nINP), .gate(INP));
  Transistor transistor_2 (.in(1'b1), .out(INP_2), .gate(nINP));
  Transistor #(.\type ("n")) transistor_3 (.in(1'b0), .out(nINP), .gate(INP));
  Transistor #(.\type ("n")) transistor_4 (.in(1'b0), .out(INP_2), .gate(nINP));

  // Notes on the sheet:
  //   S
  //   S
  //   G
  //   P
  //   D
  //   G
  //   D
  //   P
  //   G
  //   N
  //   D
  //   G
  //   N
  //   D
  //   S
  //   S
endmodule

module OR_Gate (
  input  INP0,
  input  INP1,
  output INP0___INP1
);

  wire transistor_1_out, transistor_2_out;

  Transistor transistor_1 (.in(1'b1), .out(transistor_1_out), .gate(INP1));
  Transistor transistor_2 (.in(transistor_1_out), .out(transistor_2_out), .gate(INP0));
  NOT_Gate_Inverter not_gate_inverter_1 (.INP(transistor_2_out), .nINP(INP0___INP1));
  Transistor #(.\type ("n")) transistor_3 (.in(1'b0), .out(transistor_2_out), .gate(INP1));
  Transistor #(.\type ("n")) transistor_4 (.in(1'b0), .out(transistor_2_out), .gate(INP0));

  // Notes on the sheet:
  //   A
  //   G
  //   P
  //   S
  //   D
  //   B
  //   G
  //   p
  //   S
  //   D
  //   G
  //   N
  //   D
  //   S
  //   G
  //   N
  //   D
  //   S
endmodule

module AND_Gate (
  input  INP0,
  input  INP1,
  output INP0___INP1
);

  wire transistor_1_out, transistor_4_out;

  Transistor transistor_1 (.in(1'b1), .out(transistor_1_out), .gate(INP1));
  Transistor #(.\type ("n")) transistor_2 (.in(transistor_4_out), .out(transistor_1_out), .gate(INP1));
  Transistor transistor_3 (.in(1'b1), .out(transistor_1_out), .gate(INP0));
  NOT_Gate_Inverter not_gate_inverter_1 (.INP(transistor_1_out), .nINP(INP0___INP1));
  Transistor #(.\type ("n")) transistor_4 (.in(1'b0), .out(transistor_4_out), .gate(INP0));

  // Notes on the sheet:
  //   G
  //   P
  //   S
  //   D
  //   G
  //   P
  //   S
  //   D
  //   D
  //   G
  //   N
  //   D
  //   S
  //   G
  //   N
  //   S
endmodule

module NOR_Gate (
  input  INP0,
  input  INP1,
  output n_INP0___INP1
);

  wire transistor_1_out;

  Transistor transistor_1 (.in(1'b1), .out(transistor_1_out), .gate(INP1));
  Transistor transistor_2 (.in(transistor_1_out), .out(n_INP0___INP1), .gate(INP0));
  Transistor #(.\type ("n")) transistor_3 (.in(1'b0), .out(n_INP0___INP1), .gate(INP1));
  Transistor #(.\type ("n")) transistor_4 (.in(1'b0), .out(n_INP0___INP1), .gate(INP0));

  // Notes on the sheet:
  //   S
  //   A
  //   B
  //   G
  //   G
  //   p
  //   P
  //   S
  //   D
  //   D
  //   G
  //   S
  //   D
  //   N
  //   G
  //   N
  //   D
  //   S
endmodule

module NAND_Gate (
  input  INP0,
  input  INP1,
  output n_INP0___INP1
);

  wire transistor_3_out;

  Transistor transistor_1 (.in(1'b1), .out(n_INP0___INP1), .gate(INP1));
  Transistor transistor_2 (.in(1'b1), .out(n_INP0___INP1), .gate(INP0));
  Transistor #(.\type ("n")) transistor_3 (.in(n_INP0___INP1), .out(transistor_3_out), .gate(INP1));
  Transistor #(.\type ("n")) transistor_4 (.in(1'b0), .out(transistor_3_out), .gate(INP0));

  // Notes on the sheet:
  //   G
  //   P
  //   S
  //   D
  //   G
  //   P
  //   D
  //   S
  //   G
  //   N
  //   D
  //   S
  //   G
  //   N
  //   D
  //   S
endmodule

module XOR_Gate (
  input  INP0,
  input  INP1,
  output INP0_XOR_INP
);

  wire buffer_1_inp_2, buffer_1_ninp, INP1_t, nINP1, transistor_1_out, transistor_2_out, transistor_7_out;

  BUFFER buffer_1 (.INP(INP0), .nINP(buffer_1_ninp), .INP_2(buffer_1_inp_2));
  BUFFER buffer_2 (.INP(INP1), .nINP(nINP1), .INP_2(INP1_t));
  Transistor transistor_1 (.in(1'b1), .out(transistor_1_out), .gate(buffer_1_inp_2));
  Transistor transistor_2 (.in(1'b1), .out(transistor_2_out), .gate(buffer_1_ninp));
  Transistor transistor_3 (.in(transistor_1_out), .out(INP0_XOR_INP), .gate(nINP1));
  Transistor transistor_4 (.in(transistor_2_out), .out(INP0_XOR_INP), .gate(INP1_t));
  Transistor #(.\type ("n")) transistor_5 (.in(transistor_7_out), .out(INP0_XOR_INP), .gate(buffer_1_inp_2));
  Transistor #(.\type ("n")) transistor_6 (.in(transistor_7_out), .out(INP0_XOR_INP), .gate(nINP1));
  Transistor #(.\type ("n")) transistor_7 (.in(1'b0), .out(transistor_7_out), .gate(INP1_t));
  Transistor #(.\type ("n")) transistor_8 (.in(1'b0), .out(transistor_7_out), .gate(buffer_1_ninp));

  // Notes on the sheet:
  //   G
  //   P
  //   S
  //   G
  //   P
  //   S
  //   D
  //   G
  //   G
  //   P
  //   S
  //   D
  //   G
  //   P
  //   S
  //   D
  //   D
  //   G
  //   N
  //   D
  //   G
  //   N
  //   D
  //   S
  //   S
  //   G
  //   N
  //   D
  //   G
  //   N
  //   S
  //   D
  //   S
endmodule

module XNOR_Gate (
  input  INP0,
  input  INP1,
  output INP0_XNOR_INP1
);

  wire buffer_1_inp_2, buffer_1_ninp, INP1_t, nINP1, transistor_1_out, transistor_2_out, transistor_3_out,
       transistor_7_out;

  BUFFER buffer_1 (.INP(INP0), .nINP(buffer_1_ninp), .INP_2(buffer_1_inp_2));
  BUFFER buffer_2 (.INP(INP1), .nINP(nINP1), .INP_2(INP1_t));
  Transistor transistor_1 (.in(1'b1), .out(transistor_1_out), .gate(buffer_1_inp_2));
  Transistor transistor_2 (.in(1'b1), .out(transistor_2_out), .gate(buffer_1_ninp));
  Transistor transistor_3 (.in(transistor_1_out), .out(transistor_3_out), .gate(nINP1));
  Transistor transistor_4 (.in(transistor_2_out), .out(transistor_3_out), .gate(INP1_t));
  Transistor #(.\type ("n")) transistor_5 (.in(transistor_7_out), .out(transistor_3_out), .gate(buffer_1_inp_2));
  Transistor #(.\type ("n")) transistor_6 (.in(transistor_7_out), .out(transistor_3_out), .gate(nINP1));
  Transistor #(.\type ("n")) transistor_7 (.in(1'b0), .out(transistor_7_out), .gate(INP1_t));
  Transistor #(.\type ("n")) transistor_8 (.in(1'b0), .out(transistor_7_out), .gate(buffer_1_ninp));
  NOT_Gate_Inverter not_gate_inverter_1 (.INP(transistor_3_out), .nINP(INP0_XNOR_INP1));

  // Notes on the sheet:
  //   P
  //   S
  //   P
  //   S
  //   D
  //   P
  //   S
  //   D
  //   P
  //   S
  //   D
  //   D
  //   N
  //   D
  //   N
  //   D
  //   S
  //   S
  //   N
  //   D
  //   N
  //   D
  //   S
  //   S
endmodule
