// Logisim project ImportantImplementations.circ as structural Verilog
module F_A__B_____AB_With_CMOS (
  input  A,
  input  B,
  output F
);

  wire not_1_out, transistor_1_out;

  not not_1 (not_1_out, B);
  Transistor transistor_1 (.in(1'b1), .out(transistor_1_out), .gate(A));
  Transistor transistor_2 (.in(transistor_1_out), .out(F), .gate(not_1_out));
  Transistor #(.\type ("n")) transistor_3 (.in(1'b0), .out(F), .gate(A));
  Transistor #(.\type ("n")) transistor_4 (.in(1'b0), .out(F), .gate(not_1_out));
endmodule

module _1____3____2____5____4_Synchronous_Counter (
  input  in_1,
  input  in_2,
  input  in_3,
  output out_4,
  output out_5,
  output out_6
);

  wire A_qn, and_1_out, and_2_out, and_3_out, B_qn, C_qn, clock_1_out, or_1_out;

  J_K_Flip_Flop A (
    .J(and_2_out), .clk(clock_1_out), .K(and_1_out), .Q(out_4), .Qn(A_qn), .preset(in_1), .en(in_2),
    .reset(in_3));
  Clock clock_1 (.out(clock_1_out));
  and and_1 (and_1_out, out_4, B_qn, C_qn);
  and and_2 (and_2_out, A_qn, out_5, C_qn);
  or or_1 (or_1_out, out_4, out_5);
  and and_3 (and_3_out, A_qn, out_6);
  J_K_Flip_Flop B (
    .J(and_3_out), .clk(clock_1_out), .K(and_2_out), .Q(out_5), .Qn(B_qn), .preset(in_1), .en(in_2),
    .reset(in_3));
  J_K_Flip_Flop C (
    .J(1'b1), .clk(clock_1_out), .K(or_1_out), .Q(out_6), .Qn(C_qn), .preset(in_1), .en(in_2), .reset(in_3));
endmodule

module _8x8_ROM_For_7_Segment_Display_with_3x8_Decoder (
  input  B2,
  input  B1,
  input  B0,
  output P0,
  output P1,
  output P2,
  output P3,
  output P4,
  output P5,
  output P6,
  output P7
);

  wire n3_8_line_decoder_demutiplexer_1_d0, n3_8_line_decoder_demutiplexer_1_d1,
       n3_8_line_decoder_demutiplexer_1_d2, n3_8_line_decoder_demutiplexer_1_d3,
       n3_8_line_decoder_demutiplexer_1_d4, n3_8_line_decoder_demutiplexer_1_d5,
       n3_8_line_decoder_demutiplexer_1_d6, n3_8_line_decoder_demutiplexer_1_d7;

  not not_1 (P0, 1'b1);
  _3_8_Line_Decoder_Demutiplexer u_3_8_line_decoder_demutiplexer_1 (
    .En(1'b1), .D0(n3_8_line_decoder_demutiplexer_1_d0), .D1(n3_8_line_decoder_demutiplexer_1_d1),
    .D2(n3_8_line_decoder_demutiplexer_1_d2), .D3(n3_8_line_decoder_demutiplexer_1_d3),
    .D4(n3_8_line_decoder_demutiplexer_1_d4), .D5(n3_8_line_decoder_demutiplexer_1_d5),
    .D6(n3_8_line_decoder_demutiplexer_1_d6), .D7(n3_8_line_decoder_demutiplexer_1_d7), .B2(B2), .B1(B1),
    .B0(B0));
  or or_1 (P1, n3_8_line_decoder_demutiplexer_1_d0, n3_8_line_decoder_demutiplexer_1_d1, n3_8_line_decoder_demutiplexer_1_d3, n3_8_line_decoder_demutiplexer_1_d4, n3_8_line_decoder_demutiplexer_1_d5, n3_8_line_decoder_demutiplexer_1_d6, n3_8_line_decoder_demutiplexer_1_d7);
  or or_2 (P2, n3_8_line_decoder_demutiplexer_1_d0, n3_8_line_decoder_demutiplexer_1_d2, n3_8_line_decoder_demutiplexer_1_d3, n3_8_line_decoder_demutiplexer_1_d5, n3_8_line_decoder_demutiplexer_1_d6);
  or or_3 (P3, n3_8_line_decoder_demutiplexer_1_d0, n3_8_line_decoder_demutiplexer_1_d2, n3_8_line_decoder_demutiplexer_1_d6);
  or or_4 (P4, n3_8_line_decoder_demutiplexer_1_d2, n3_8_line_decoder_demutiplexer_1_d3, n3_8_line_decoder_demutiplexer_1_d4, n3_8_line_decoder_demutiplexer_1_d5, n3_8_line_decoder_demutiplexer_1_d6);
  or or_5 (P5, n3_8_line_decoder_demutiplexer_1_d0, n3_8_line_decoder_demutiplexer_1_d4, n3_8_line_decoder_demutiplexer_1_d5, n3_8_line_decoder_demutiplexer_1_d6);
  or or_6 (P6, n3_8_line_decoder_demutiplexer_1_d0, n3_8_line_decoder_demutiplexer_1_d2, n3_8_line_decoder_demutiplexer_1_d3, n3_8_line_decoder_demutiplexer_1_d5, n3_8_line_decoder_demutiplexer_1_d6, n3_8_line_decoder_demutiplexer_1_d7);
  or or_7 (P7, n3_8_line_decoder_demutiplexer_1_d0, n3_8_line_decoder_demutiplexer_1_d1, n3_8_line_decoder_demutiplexer_1_d2, n3_8_line_decoder_demutiplexer_1_d3, n3_8_line_decoder_demutiplexer_1_d4, n3_8_line_decoder_demutiplexer_1_d7);
endmodule

module ROM_For_Segment_Display_Octal_Output_Demo (
  input  in_1,
  input  in_2,
  input  in_3
);

  wire n8x8_rom_for_7_segment_display_with_3x8_decoder_1_p0,
       n8x8_rom_for_7_segment_display_with_3x8_decoder_1_p1,
       n8x8_rom_for_7_segment_display_with_3x8_decoder_1_p2,
       n8x8_rom_for_7_segment_display_with_3x8_decoder_1_p3,
       n8x8_rom_for_7_segment_display_with_3x8_decoder_1_p4,
       n8x8_rom_for_7_segment_display_with_3x8_decoder_1_p5,
       n8x8_rom_for_7_segment_display_with_3x8_decoder_1_p6,
       n8x8_rom_for_7_segment_display_with_3x8_decoder_1_p7;

  _8x8_ROM_For_7_Segment_Display_with_3x8_Decoder u_8x8_rom_for_7_segment_display_with_3x8_decoder_1 (
    .P0(n8x8_rom_for_7_segment_display_with_3x8_decoder_1_p0),
    .P1(n8x8_rom_for_7_segment_display_with_3x8_decoder_1_p1),
    .P2(n8x8_rom_for_7_segment_display_with_3x8_decoder_1_p2),
    .P3(n8x8_rom_for_7_segment_display_with_3x8_decoder_1_p3),
    .P4(n8x8_rom_for_7_segment_display_with_3x8_decoder_1_p4),
    .P5(n8x8_rom_for_7_segment_display_with_3x8_decoder_1_p5),
    .P6(n8x8_rom_for_7_segment_display_with_3x8_decoder_1_p6),
    .P7(n8x8_rom_for_7_segment_display_with_3x8_decoder_1_p7), .B2(in_1), .B1(in_2), .B0(in_3));
  _7_Segment_Display u_7_segment_display_1 (
    .g(n8x8_rom_for_7_segment_display_with_3x8_decoder_1_p4),
    .f(n8x8_rom_for_7_segment_display_with_3x8_decoder_1_p5),
    .a(n8x8_rom_for_7_segment_display_with_3x8_decoder_1_p6),
    .b(n8x8_rom_for_7_segment_display_with_3x8_decoder_1_p7),
    .e(n8x8_rom_for_7_segment_display_with_3x8_decoder_1_p3),
    .d(n8x8_rom_for_7_segment_display_with_3x8_decoder_1_p2),
    .c(n8x8_rom_for_7_segment_display_with_3x8_decoder_1_p1),
    .dp(n8x8_rom_for_7_segment_display_with_3x8_decoder_1_p0));
endmodule

module Cascaded_Decoders (
  input  B3,
  input  B2,
  input  B1,
  input  B0,
  output D15,
  output D14,
  output D13,
  output D12,
  output D11,
  output D10,
  output D9,
  output D8,
  output D7,
  output D6,
  output D5,
  output D4,
  output D3,
  output D2,
  output D1,
  output D0
);

  wire not_1_out;

  _3_8_Line_Decoder_Demutiplexer u_3_8_line_decoder_demutiplexer_1 (
    .En(not_1_out), .D0(D0), .D1(D1), .D2(D2), .D3(D3), .D4(D4), .D5(D5), .D6(D6), .D7(D7), .B2(B2), .B1(B1),
    .B0(B0));
  not not_1 (not_1_out, B3);
  _3_8_Line_Decoder_Demutiplexer u_3_8_line_decoder_demutiplexer_2 (
    .En(B3), .D0(D8), .D1(D9), .D2(D10), .D3(D11), .D4(D12), .D5(D13), .D6(D14), .D7(D15), .B2(B2), .B1(B1),
    .B0(B0));
endmodule

module Boolean_Function_implementation_with_Multiplexer (
  input  Enable,
  input  A,
  input  B,
  input  C,
  output F
);

  wire not_1_out, not_2_out;

  not not_1 (not_1_out, 1'b1);
  _4_1_MUltiplexer u_4_1_multiplexer_1 (
    .Input0(not_1_out), .Input1(1'b1), .Input2(A), .Input3(not_2_out), .Output(F), .En(Enable), .S1(B), .S0(C));
  not not_2 (not_2_out, A);

  // Notes on the sheet:
  //   F(A, B, C) = Sum(1, 3, 5, 6)
endmodule

module Boolean_Function_imolementation_with_Decoder (
  input  Enable,
  input  C,
  input  B,
  input  A,
  output F
);

  wire n3_8_line_decoder_demutiplexer_1_d1, n3_8_line_decoder_demutiplexer_1_d3,
       n3_8_line_decoder_demutiplexer_1_d5, n3_8_line_decoder_demutiplexer_1_d6;

  _3_8_Line_Decoder_Demutiplexer u_3_8_line_decoder_demutiplexer_1 (
    .En(Enable), .D1(n3_8_line_decoder_demutiplexer_1_d1), .D3(n3_8_line_decoder_demutiplexer_1_d3),
    .D5(n3_8_line_decoder_demutiplexer_1_d5), .D6(n3_8_line_decoder_demutiplexer_1_d6), .B2(C), .B1(B), .B0(A));  // open: D0, D2, D4, D7
  or or_1 (F, n3_8_line_decoder_demutiplexer_1_d1, n3_8_line_decoder_demutiplexer_1_d3, n3_8_line_decoder_demutiplexer_1_d5, n3_8_line_decoder_demutiplexer_1_d6);

  // Notes on the sheet:
  //   F(A, B, C) = Sum(1, 3, 5, 6)
endmodule

module Cascaded_Synchronous_Counter (
  input  in_1,
  input  in_2,
  output [7:0] out_3
);

  wire clock_1_out, n4_bit_binary_synchronous_up_counter_jk_ff_1_next;

  Clock clock_1 (.out(clock_1_out));
  _4_Bit_Binary_Synchronous_Up_Counter_JK_FF u_4_bit_binary_synchronous_up_counter_jk_ff_1 (
    .Clk(clock_1_out), .CountEn(in_1), .En(in_2), .Next(n4_bit_binary_synchronous_up_counter_jk_ff_1_next),
    .A3(out_3[3]), .A2(out_3[2]), .A1(out_3[1]), .A0(out_3[0]));  // open: Preset, Clear
  _4_Bit_Binary_Synchronous_Up_Counter_JK_FF u_4_bit_binary_synchronous_up_counter_jk_ff_2 (
    .Clk(clock_1_out), .CountEn(n4_bit_binary_synchronous_up_counter_jk_ff_1_next), .En(in_2), .A3(out_3[7]),
    .A2(out_3[6]), .A1(out_3[5]), .A0(out_3[4]));  // open: Preset, Clear, Next
endmodule
