// Logisim project ProcessorUnit.circ as structural Verilog
module _4_Bit_Arithmetiic_Circuit (
  input  [3:0] B,
  input  [3:0] A,
  input  S1,
  input  S0,
  input  Cin,
  output [4:0] F
);

  wire full_adder_2_cout, full_adder_3_cout, full_adder_4_cout, true_complement_circuit_1_y,
       true_complement_circuit_2_y, true_complement_circuit_3_y, true_complement_circuit_4_y;

  True_Complement_Circuit true_complement_circuit_1 (.B(B[3]), .S1(S1), .S0(S0), .Y(true_complement_circuit_1_y));
  Full_Adder full_adder_1 (.Cout(F[4]), .Cin(full_adder_2_cout), .Y(true_complement_circuit_1_y), .X(A[3]), .Sum(F[3]));
  True_Complement_Circuit true_complement_circuit_2 (.B(B[2]), .S1(S1), .S0(S0), .Y(true_complement_circuit_2_y));
  True_Complement_Circuit true_complement_circuit_3 (.B(B[1]), .S1(S1), .S0(S0), .Y(true_complement_circuit_3_y));
  Full_Adder full_adder_2 (
    .Cout(full_adder_2_cout), .Cin(full_adder_3_cout), .Y(true_complement_circuit_2_y), .X(A[2]), .Sum(F[2]));
  True_Complement_Circuit true_complement_circuit_4 (.B(B[0]), .S1(S1), .S0(S0), .Y(true_complement_circuit_4_y));
  Full_Adder full_adder_3 (
    .Cout(full_adder_3_cout), .Cin(full_adder_4_cout), .Y(true_complement_circuit_3_y), .X(A[1]), .Sum(F[1]));
  Full_Adder full_adder_4 (.Cout(full_adder_4_cout), .Cin(Cin), .Y(true_complement_circuit_4_y), .X(A[0]), .Sum(F[0]));
endmodule

// F/A
module Full_Adder (
  input  Y,
  input  X,
  input  Cin,
  output Cout,
  output Sum
);

  wire and_1_out, and_2_out, xor_1_out;

  xor xor_1 (xor_1_out, X, Y);
  xor xor_2 (Sum, xor_1_out, Cin);
  and and_1 (and_1_out, xor_1_out, Cin);
  and and_2 (and_2_out, X, Y);
  or or_1 (Cout, and_1_out, and_2_out);
endmodule

// 1/0
module True_Complement_Circuit (
  input  B,
  input  S1,
  input  S0,
  output Y
);

  wire and_1_out, and_2_out, not_1_out;

  not not_1 (not_1_out, B);
  and and_1 (and_1_out, S0, B);
  and and_2 (and_2_out, S1, not_1_out);
  or or_1 (Y, and_2_out, and_1_out);
endmodule

// ALU Single
module ALU_Single_Stage (
  input  B,
  input  A,
  input  S2,
  input  S1,
  input  S0,
  input  Cin,
  output S0_2,
  output S1_2,
  output S2_2,
  output Cout,
  output F
);

  wire and_1_out, and_2_out, and_3_out, or_1_out, true_complement_circuit_1_y, true_complement_circuit_2_y;

  True_Complement_Circuit true_complement_circuit_1 (.B(B), .S1(S1), .S0(S0), .Y(true_complement_circuit_1_y));
  True_Complement_Circuit true_complement_circuit_2 (
    .B(B), .S1(and_2_out), .S0(and_3_out), .Y(true_complement_circuit_2_y));
  or or_1 (or_1_out, A, true_complement_circuit_2_y);
  and and_1 (and_1_out, ~S2, Cin);  // AND_Gate
  Full_Adder full_adder_1 (.Cout(Cout), .Cin(and_1_out), .Y(true_complement_circuit_1_y), .X(or_1_out), .Sum(F));
  and and_2 (and_2_out, S2, S1, ~S0);  // AND_Gate
  and and_3 (and_3_out, S2, ~S1, ~S0);  // AND_Gate

  assign S0_2 = S0;
  assign S1_2 = S1;
  assign S2_2 = S2;
endmodule

// ALU
module _4_Bit_ALU (
  input  [3:0] B,
  input  [3:0] A,
  input  S2,
  input  S1,
  input  S0,
  input  Cin,
  output Cn_1,
  output Cout,
  output [3:0] F
);

  wire alu_single_stage_2_s0_2, alu_single_stage_2_s1_2, alu_single_stage_2_s2_2, alu_single_stage_3_cout,
       alu_single_stage_3_s0_2, alu_single_stage_3_s1_2, alu_single_stage_3_s2_2, alu_single_stage_4_cout,
       alu_single_stage_4_s0_2, alu_single_stage_4_s1_2, alu_single_stage_4_s2_2;

  ALU_Single_Stage alu_single_stage_1 (
    .Cout(Cout), .B(B[3]), .A(A[3]), .S2(alu_single_stage_2_s2_2), .S1(alu_single_stage_2_s1_2),
    .S0(alu_single_stage_2_s0_2), .Cin(Cn_1), .F(F[3]));  // open: S0_2, S1_2, S2_2
  ALU_Single_Stage alu_single_stage_2 (
    .S0_2(alu_single_stage_2_s0_2), .S1_2(alu_single_stage_2_s1_2), .S2_2(alu_single_stage_2_s2_2),
    .Cout(Cn_1), .B(B[2]), .A(A[2]), .S2(alu_single_stage_3_s2_2), .S1(alu_single_stage_3_s1_2),
    .S0(alu_single_stage_3_s0_2), .Cin(alu_single_stage_3_cout), .F(F[2]));
  ALU_Single_Stage alu_single_stage_3 (
    .S0_2(alu_single_stage_3_s0_2), .S1_2(alu_single_stage_3_s1_2), .S2_2(alu_single_stage_3_s2_2),
    .Cout(alu_single_stage_3_cout), .B(B[1]), .A(A[1]), .S2(alu_single_stage_4_s2_2),
    .S1(alu_single_stage_4_s1_2), .S0(alu_single_stage_4_s0_2), .Cin(alu_single_stage_4_cout), .F(F[1]));
  ALU_Single_Stage alu_single_stage_4 (
    .S0_2(alu_single_stage_4_s0_2), .S1_2(alu_single_stage_4_s1_2), .S2_2(alu_single_stage_4_s2_2),
    .Cout(alu_single_stage_4_cout), .B(B[0]), .A(A[0]), .S2(S2), .S1(S1), .S0(S0), .Cin(Cin), .F(F[0]));
endmodule

// Shftr
module _4_Bit_Shifter (
  input  [3:0] A,
  input  S0,
  input  S1,
  output [3:0] F
);

  wire not_1_out;

  Multiplexer #(.select(2)) multiplexer_1 (
    .in0(A[3]), .in3(not_1_out), .out(F[3]), .sel({S1, S0}));  // open: in1, in2, en
  Multiplexer #(.select(2)) multiplexer_2 (
    .in0(A[2]), .in3(not_1_out), .out(F[2]), .sel({S1, S0}));  // open: in1, in2, en
  Multiplexer #(.select(2)) multiplexer_3 (
    .in0(A[1]), .in3(not_1_out), .out(F[1]), .sel({S1, S0}));  // open: in1, in2, en
  Multiplexer #(.select(2)) multiplexer_4 (
    .in0(A[0]), .in3(not_1_out), .out(F[0]), .sel({S1, S0}));  // open: in1, in2, en
  not not_1 (not_1_out, 1'b1);

  // Other names for the same wires on the sheet: Select[1:0] = {S1, S0}
endmodule

module Processor_Unit (
  input  [3:0] InpB,
  input  [3:0] InpA,
  input  [2:0] D,
  input  [2:0] A,
  input  [2:0] B,
  input  [2:0] F,
  input  Cin,
  input  [1:0] H,
  output [3:0] out_9,
  output [3:0] Output
);

  wire clock_1_out, n4_bit_alu_1_cn_1, n4_bit_alu_1_cout;
  wire [3:0] multiplexer_1_out, multiplexer_2_out, n4_bit_alu_1_f, n7_register_file_1_r1,
       n7_register_file_1_r2, n7_register_file_1_r3, n7_register_file_1_r4, n7_register_file_1_r5,
       n7_register_file_1_r6, n7_register_file_1_r7;
  wire [6:0] decoder_1_out1;

  Clock clock_1 (.out(clock_1_out));
  Decoder #(.select(3)) decoder_1 (
    .out1(decoder_1_out1[0]), .out2(decoder_1_out1[1]), .out3(decoder_1_out1[2]), .out4(decoder_1_out1[3]),
    .out5(decoder_1_out1[4]), .out6(decoder_1_out1[5]), .out7(decoder_1_out1[6]), .sel(D));  // open: out0, en
  _7_Register_File u_7_register_file_1 (
    .Data(Output), .Clk(clock_1_out), .En(decoder_1_out1), .R1(n7_register_file_1_r1),
    .R2(n7_register_file_1_r2), .R3(n7_register_file_1_r3), .R4(n7_register_file_1_r4),
    .R5(n7_register_file_1_r5), .R6(n7_register_file_1_r6), .R7(n7_register_file_1_r7));
  Multiplexer #(.select(3), .width(4)) multiplexer_1 (
    .in0(InpB), .in1(n7_register_file_1_r1), .in2(n7_register_file_1_r2), .in3(n7_register_file_1_r3),
    .in4(n7_register_file_1_r4), .in5(n7_register_file_1_r5), .in6(n7_register_file_1_r6),
    .in7(n7_register_file_1_r7), .out(multiplexer_1_out), .sel(A));  // open: en
  Status_Register status_register_1 (
    .Clk(clock_1_out), .out_5(out_9), .Cn_1(n4_bit_alu_1_cn_1), .Cout(n4_bit_alu_1_cout),
    .ALU_Output(n4_bit_alu_1_f));
  _4_Bit_ALU u_4_bit_alu_1 (
    .Cn_1(n4_bit_alu_1_cn_1), .B(multiplexer_1_out), .A(multiplexer_2_out), .Cout(n4_bit_alu_1_cout),
    .F(n4_bit_alu_1_f), .S2(F[2]), .S1(F[1]), .S0(F[0]), .Cin(Cin));
  _4_Bit_Shifter u_4_bit_shifter_1 (.S0(H[0]), .S1(H[1]), .A(n4_bit_alu_1_f), .F(Output));
  Multiplexer #(.select(3), .width(4)) multiplexer_2 (
    .in0(InpA), .in1(n7_register_file_1_r1), .in2(n7_register_file_1_r2), .in3(n7_register_file_1_r3),
    .in4(n7_register_file_1_r4), .in5(n7_register_file_1_r5), .in6(n7_register_file_1_r6),
    .in7(n7_register_file_1_r7), .out(multiplexer_2_out), .sel(B));  // open: en
endmodule

// Register File
module _7_Register_File (
  input  [3:0] Data,
  input  Clk,
  input  [6:0] En,
  output [3:0] R1,
  output [3:0] R2,
  output [3:0] R3,
  output [3:0] R4,
  output [3:0] R5,
  output [3:0] R6,
  output [3:0] R7
);

  Register #(.width(4)) register_1 (.D(Data), .en(En[0]), .Q(R1), .clk(Clk));  // open: clr
  Register #(.width(4)) register_2 (.D(Data), .en(En[1]), .Q(R2), .clk(Clk));  // open: clr
  Register #(.width(4)) register_3 (.D(Data), .en(En[2]), .Q(R3), .clk(Clk));  // open: clr
  Register #(.width(4)) register_4 (.D(Data), .en(En[3]), .Q(R4), .clk(Clk));  // open: clr
  Register #(.width(4)) register_5 (.D(Data), .en(En[4]), .Q(R5), .clk(Clk));  // open: clr
  Register #(.width(4)) register_6 (.D(Data), .en(En[5]), .Q(R6), .clk(Clk));  // open: clr
  Register #(.width(4)) register_7 (.D(Data), .en(En[6]), .Q(R7), .clk(Clk));  // open: clr
endmodule

// StatusReg
module Status_Register (
  input  Cn_1,
  input  Cout,
  input  [3:0] ALU_Output,
  input  Clk,
  output [3:0] out_5
);

  wire [3:2] nor_1_out;

  nor nor_1 (nor_1_out[2], ALU_Output[0], ALU_Output[1], ALU_Output[2], ALU_Output[3]);
  Register #(.width(4)) register_1 (.D({nor_1_out, ALU_Output[0], Cout}), .Q(out_5), .clk(Clk));  // open: en, clr
  xor xor_1 (nor_1_out[3], Cn_1, Cout);
endmodule
