// Logisim project RAM.circ as structural Verilog: 8 circuits, main circuit main
module main (
  input  Clear_Screen,
  input  in_2,
  input  in_3,
  input  En,
  input  nW_R,
  input  [1:0] in_6,
  input  in_7,
  input  En_2,
  input  in_9,
  input  nW_R_2,
  input  S1,
  input  S0
);

  wire Clk_out, clock_1_out, MBR_out_10, MBR_out_11, MBR_out_12, MBR_out_13, MBR_out_14, MBR_out_15,
       MBR_out_16, or_1_out;
  wire [6:0] keyboard_1_data, keyboard_2_data, Output, Output1;

  TTY tty_1 (.data(Output), .clk(Clk_out), .clr(Clear_Screen));  // open: we
  Keyboard keyboard_1 (.clk(Clk_out), .data(keyboard_1_data));  // open: re, clr, avail
  Clock Clk (.out(Clk_out));
  _4_8_RAM u_4_8_ram_1 (
    .En(En), .nWrite_Read(nW_R), .I7(in_3), .I6(MBR_out_16), .I5(MBR_out_15), .I4(MBR_out_14),
    .I3(MBR_out_13), .I2(MBR_out_12), .I1(MBR_out_11), .I0(MBR_out_10), .S1(S1), .S0(S0), .D6(Output[6]),
    .D5(Output[5]), .D4(Output[4]), .D3(Output[3]), .D2(Output[2]), .D1(Output[1]), .D0(Output[0]));  // open: D7
  _7_Bit_PIPO MBR (
    .in_2(keyboard_1_data[0]), .in_3(keyboard_1_data[1]), .in_4(keyboard_1_data[2]),
    .in_5(keyboard_1_data[3]), .in_6(keyboard_1_data[4]), .in_7(keyboard_1_data[5]),
    .in_8(keyboard_1_data[6]), .LoadControl(or_1_out), .Clk(Clk_out), .out_10(MBR_out_10),
    .out_11(MBR_out_11), .out_12(MBR_out_12), .out_13(MBR_out_13), .out_14(MBR_out_14), .out_15(MBR_out_15),
    .out_16(MBR_out_16));
  or or_1 (or_1_out, keyboard_1_data[0], keyboard_1_data[1], keyboard_1_data[2], keyboard_1_data[3], keyboard_1_data[4], keyboard_1_data[5], keyboard_1_data[6]);
  TTY tty_2 (.data(Output1), .clk(clock_1_out), .we(En_2), .clr(in_9));
  Clock clock_1 (.out(clock_1_out));
  Keyboard keyboard_2 (.clk(clock_1_out), .data(keyboard_2_data));  // open: re, clr, avail
  Memory_Unit memory_unit_1 (
    .Clk(clock_1_out), .Preset(in_7), .En(En_2), .Clear(in_9), .nWrite_Read(nW_R_2), .I7(in_2),
    .I6(keyboard_2_data[6]), .I5(keyboard_2_data[5]), .I4(keyboard_2_data[4]), .I3(keyboard_2_data[3]),
    .I2(keyboard_2_data[2]), .I1(keyboard_2_data[1]), .I0(keyboard_2_data[0]), .S1(in_6[1]), .S0(in_6[0]),
    .D6(Output1[6]), .D5(Output1[5]), .D4(Output1[4]), .D3(Output1[3]), .D2(Output1[2]), .D1(Output1[1]),
    .D0(Output1[0]));  // open: D7
endmodule

module Binary_Cell (
  input  Select,
  input  Input,
  input  Read_Write,
  output Output
);

  wire and_1_out, and_2_out, not_1_out, not_2_out, rs_ff_nor_latch_1_out;

  not not_1 (not_1_out, Input);
  and and_1 (and_1_out, Select, not_1_out, not_2_out);
  and and_2 (and_2_out, Select, Input, not_2_out);
  not not_2 (not_2_out, Read_Write);
  RS_FF_NOR_LATCH rs_ff_nor_latch_1 (.Reset(and_1_out), .Set(and_2_out), .Out(rs_ff_nor_latch_1_out));  // open: nOut
  and and_3 (Output, Select, rs_ff_nor_latch_1_out, Read_Write);
endmodule

module _2_4_Line_Decoder_Demultiplexer (
  input  S0,
  input  S1,
  input  En,
  output D0,
  output D1,
  output D2,
  output D3
);

  and and_1 (D0, ~S0, ~S1, En);  // AND_Gate
  and and_2 (D1, ~S1, S0, En);  // AND_Gate
  and and_3 (D2, S1, ~S0, En);  // AND_Gate
  and and_4 (D3, S1, S0, En);
endmodule

module _4_8_RAM (
  input  I7,
  input  I6,
  input  I5,
  input  I4,
  input  I3,
  input  I2,
  input  I1,
  input  I0,
  input  S1,
  input  S0,
  input  En,
  input  nWrite_Read,
  output D7,
  output D6,
  output D5,
  output D4,
  output D3,
  output D2,
  output D1,
  output D0
);

  wire binary_cell_1_output, binary_cell_2_output, binary_cell_3_output, binary_cell_4_output,
       binary_cell_5_output, binary_cell_6_output, binary_cell_7_output, binary_cell_8_output,
       binary_cell_9_output, binary_cell_10_output, binary_cell_11_output, binary_cell_12_output,
       binary_cell_13_output, binary_cell_14_output, binary_cell_15_output, binary_cell_16_output,
       binary_cell_17_output, binary_cell_18_output, binary_cell_19_output, binary_cell_20_output,
       binary_cell_21_output, binary_cell_22_output, binary_cell_23_output, binary_cell_24_output,
       binary_cell_25_output, binary_cell_26_output, binary_cell_27_output, binary_cell_28_output,
       binary_cell_29_output, binary_cell_30_output, binary_cell_31_output, binary_cell_32_output,
       n2_4_line_decoder_demultiplexer_1_d0, n2_4_line_decoder_demultiplexer_1_d1,
       n2_4_line_decoder_demultiplexer_1_d2, n2_4_line_decoder_demultiplexer_1_d3;

  _2_4_Line_Decoder_Demultiplexer u_2_4_line_decoder_demultiplexer_1 (
    .S0(S0), .S1(S1), .D0(n2_4_line_decoder_demultiplexer_1_d0), .D1(n2_4_line_decoder_demultiplexer_1_d1),
    .D2(n2_4_line_decoder_demultiplexer_1_d2), .D3(n2_4_line_decoder_demultiplexer_1_d3), .En(En));
  Binary_Cell binary_cell_1 (
    .Input(I7), .Output(binary_cell_1_output), .Select(n2_4_line_decoder_demultiplexer_1_d0),
    .Read_Write(nWrite_Read));
  Binary_Cell binary_cell_2 (
    .Input(I7), .Output(binary_cell_2_output), .Select(n2_4_line_decoder_demultiplexer_1_d1),
    .Read_Write(nWrite_Read));
  Binary_Cell binary_cell_3 (
    .Input(I7), .Output(binary_cell_3_output), .Select(n2_4_line_decoder_demultiplexer_1_d2),
    .Read_Write(nWrite_Read));
  Binary_Cell binary_cell_4 (
    .Input(I7), .Output(binary_cell_4_output), .Select(n2_4_line_decoder_demultiplexer_1_d3),
    .Read_Write(nWrite_Read));
  or or_1 (D7, binary_cell_4_output, binary_cell_3_output, binary_cell_2_output, binary_cell_1_output);
  Binary_Cell binary_cell_5 (
    .Input(I6), .Output(binary_cell_5_output), .Select(n2_4_line_decoder_demultiplexer_1_d0),
    .Read_Write(nWrite_Read));
  Binary_Cell binary_cell_6 (
    .Input(I6), .Output(binary_cell_6_output), .Select(n2_4_line_decoder_demultiplexer_1_d1),
    .Read_Write(nWrite_Read));
  Binary_Cell binary_cell_7 (
    .Input(I6), .Output(binary_cell_7_output), .Select(n2_4_line_decoder_demultiplexer_1_d2),
    .Read_Write(nWrite_Read));
  Binary_Cell binary_cell_8 (
    .Input(I6), .Output(binary_cell_8_output), .Select(n2_4_line_decoder_demultiplexer_1_d3),
    .Read_Write(nWrite_Read));
  or or_2 (D6, binary_cell_8_output, binary_cell_7_output, binary_cell_6_output, binary_cell_5_output);
  Binary_Cell binary_cell_9 (
    .Input(I5), .Output(binary_cell_9_output), .Select(n2_4_line_decoder_demultiplexer_1_d0),
    .Read_Write(nWrite_Read));
  Binary_Cell binary_cell_10 (
    .Input(I5), .Output(binary_cell_10_output), .Select(n2_4_line_decoder_demultiplexer_1_d1),
    .Read_Write(nWrite_Read));
  Binary_Cell binary_cell_11 (
    .Input(I5), .Output(binary_cell_11_output), .Select(n2_4_line_decoder_demultiplexer_1_d2),
    .Read_Write(nWrite_Read));
  Binary_Cell binary_cell_12 (
    .Input(I5), .Output(binary_cell_12_output), .Select(n2_4_line_decoder_demultiplexer_1_d3),
    .Read_Write(nWrite_Read));
  or or_3 (D5, binary_cell_12_output, binary_cell_11_output, binary_cell_10_output, binary_cell_9_output);
  Binary_Cell binary_cell_13 (
    .Input(I4), .Output(binary_cell_13_output), .Select(n2_4_line_decoder_demultiplexer_1_d0),
    .Read_Write(nWrite_Read));
  Binary_Cell binary_cell_14 (
    .Input(I4), .Output(binary_cell_14_output), .Select(n2_4_line_decoder_demultiplexer_1_d1),
    .Read_Write(nWrite_Read));
  Binary_Cell binary_cell_15 (
    .Input(I4), .Output(binary_cell_15_output), .Select(n2_4_line_decoder_demultiplexer_1_d2),
    .Read_Write(nWrite_Read));
  Binary_Cell binary_cell_16 (
    .Input(I4), .Output(binary_cell_16_output), .Select(n2_4_line_decoder_demultiplexer_1_d3),
    .Read_Write(nWrite_Read));
  or or_4 (D4, binary_cell_16_output, binary_cell_15_output, binary_cell_14_output, binary_cell_13_output);
  Binary_Cell binary_cell_17 (
    .Input(I3), .Output(binary_cell_17_output), .Select(n2_4_line_decoder_demultiplexer_1_d0),
    .Read_Write(nWrite_Read));
  Binary_Cell binary_cell_18 (
    .Input(I3), .Output(binary_cell_18_output), .Select(n2_4_line_decoder_demultiplexer_1_d1),
    .Read_Write(nWrite_Read));
  Binary_Cell binary_cell_19 (
    .Input(I3), .Output(binary_cell_19_output), .Select(n2_4_line_decoder_demultiplexer_1_d2),
    .Read_Write(nWrite_Read));
  Binary_Cell binary_cell_20 (
    .Input(I3), .Output(binary_cell_20_output), .Select(n2_4_line_decoder_demultiplexer_1_d3),
    .Read_Write(nWrite_Read));
  or or_5 (D3, binary_cell_20_output, binary_cell_19_output, binary_cell_18_output, binary_cell_17_output);
  Binary_Cell binary_cell_21 (
    .Input(I2), .Output(binary_cell_21_output), .Select(n2_4_line_decoder_demultiplexer_1_d0),
    .Read_Write(nWrite_Read));
  Binary_Cell binary_cell_22 (
    .Input(I2), .Output(binary_cell_22_output), .Select(n2_4_line_decoder_demultiplexer_1_d1),
    .Read_Write(nWrite_Read));
  Binary_Cell binary_cell_23 (
    .Input(I2), .Output(binary_cell_23_output), .Select(n2_4_line_decoder_demultiplexer_1_d2),
    .Read_Write(nWrite_Read));
  Binary_Cell binary_cell_24 (
    .Input(I2), .Output(binary_cell_24_output), .Select(n2_4_line_decoder_demultiplexer_1_d3),
    .Read_Write(nWrite_Read));
  or or_6 (D2, binary_cell_24_output, binary_cell_23_output, binary_cell_22_output, binary_cell_21_output);
  Binary_Cell binary_cell_25 (
    .Input(I1), .Output(binary_cell_25_output), .Select(n2_4_line_decoder_demultiplexer_1_d0),
    .Read_Write(nWrite_Read));
  Binary_Cell binary_cell_26 (
    .Input(I1), .Output(binary_cell_26_output), .Select(n2_4_line_decoder_demultiplexer_1_d1),
    .Read_Write(nWrite_Read));
  Binary_Cell binary_cell_27 (
    .Input(I1), .Output(binary_cell_27_output), .Select(n2_4_line_decoder_demultiplexer_1_d2),
    .Read_Write(nWrite_Read));
  Binary_Cell binary_cell_28 (
    .Input(I1), .Output(binary_cell_28_output), .Select(n2_4_line_decoder_demultiplexer_1_d3),
    .Read_Write(nWrite_Read));
  or or_7 (D1, binary_cell_28_output, binary_cell_27_output, binary_cell_26_output, binary_cell_25_output);
  Binary_Cell binary_cell_29 (
    .Input(I0), .Output(binary_cell_29_output), .Select(n2_4_line_decoder_demultiplexer_1_d0),
    .Read_Write(nWrite_Read));
  Binary_Cell binary_cell_30 (
    .Input(I0), .Output(binary_cell_30_output), .Select(n2_4_line_decoder_demultiplexer_1_d1),
    .Read_Write(nWrite_Read));
  Binary_Cell binary_cell_31 (
    .Input(I0), .Output(binary_cell_31_output), .Select(n2_4_line_decoder_demultiplexer_1_d2),
    .Read_Write(nWrite_Read));
  Binary_Cell binary_cell_32 (
    .Input(I0), .Output(binary_cell_32_output), .Select(n2_4_line_decoder_demultiplexer_1_d3),
    .Read_Write(nWrite_Read));
  or or_8 (D0, binary_cell_32_output, binary_cell_31_output, binary_cell_30_output, binary_cell_29_output);
endmodule

module _7_Bit_PIPO (
  input  LoadControl,
  input  in_2,
  input  in_3,
  input  in_4,
  input  in_5,
  input  in_6,
  input  in_7,
  input  in_8,
  input  Clk,
  output out_10,
  output out_11,
  output out_12,
  output out_13,
  output out_14,
  output out_15,
  output out_16
);

  wire and_1_out, and_2_out, and_3_out, and_4_out, and_5_out, and_6_out, and_7_out, and_8_out, and_9_out,
       and_10_out, and_11_out, and_12_out, and_13_out, and_14_out, not_1_out, not_2_out, or_1_out, or_2_out,
       or_3_out, or_4_out, or_5_out, or_6_out, or_7_out;

  not not_1 (not_1_out, LoadControl);
  not not_2 (not_2_out, not_1_out);
  and and_1 (and_1_out, out_10, not_1_out);
  and and_2 (and_2_out, in_2, not_2_out);
  and and_3 (and_3_out, out_11, not_1_out);
  and and_4 (and_4_out, in_3, not_2_out);
  and and_5 (and_5_out, out_12, not_1_out);
  and and_6 (and_6_out, in_4, not_2_out);
  and and_7 (and_7_out, out_13, not_1_out);
  and and_8 (and_8_out, in_5, not_2_out);
  and and_9 (and_9_out, out_14, not_1_out);
  and and_10 (and_10_out, in_6, not_2_out);
  and and_11 (and_11_out, out_15, not_1_out);
  and and_12 (and_12_out, in_7, not_2_out);
  and and_13 (and_13_out, out_16, not_1_out);
  and and_14 (and_14_out, in_8, not_2_out);
  or or_1 (or_1_out, and_1_out, and_2_out);
  or or_2 (or_2_out, and_3_out, and_4_out);
  or or_3 (or_3_out, and_5_out, and_6_out);
  or or_4 (or_4_out, and_7_out, and_8_out);
  or or_5 (or_5_out, and_9_out, and_10_out);
  or or_6 (or_6_out, and_11_out, and_12_out);
  or or_7 (or_7_out, and_13_out, and_14_out);
  D_Flip_Flop d_ff_1 (.clk(Clk), .D(or_1_out), .Q(out_10));  // open: Qn, preset, en, reset
  D_Flip_Flop d_ff_2 (.clk(Clk), .D(or_2_out), .Q(out_11));  // open: Qn, preset, en, reset
  D_Flip_Flop d_ff_3 (.clk(Clk), .D(or_3_out), .Q(out_12));  // open: Qn, preset, en, reset
  D_Flip_Flop d_ff_4 (.clk(Clk), .D(or_4_out), .Q(out_13));  // open: Qn, preset, en, reset
  D_Flip_Flop d_ff_5 (.clk(Clk), .D(or_5_out), .Q(out_14));  // open: Qn, preset, en, reset
  D_Flip_Flop d_ff_6 (.clk(Clk), .D(or_6_out), .Q(out_15));  // open: Qn, preset, en, reset
  D_Flip_Flop d_ff_7 (.clk(Clk), .D(or_7_out), .Q(out_16));  // open: Qn, preset, en, reset
endmodule

module Memory_Unit (
  input  I7,
  input  I6,
  input  I5,
  input  I4,
  input  I3,
  input  I2,
  input  I1,
  input  I0,
  input  Clk,
  input  Preset,
  input  En,
  input  Clear,
  input  nWrite_Read,
  input  S1,
  input  S0,
  output D7,
  output D6,
  output D5,
  output D4,
  output D3,
  output D2,
  output D1,
  output D0
);

  wire and_1_out, and_2_out, and_3_out, and_4_out, and_5_out, and_6_out, and_7_out, and_8_out, and_9_out,
       and_10_out, and_11_out, and_12_out, and_13_out, and_14_out, and_15_out, and_16_out,
       binary_cell_1_output, binary_cell_2_output, binary_cell_3_output, binary_cell_4_output,
       binary_cell_5_output, binary_cell_6_output, binary_cell_7_output, binary_cell_8_output,
       binary_cell_9_output, binary_cell_10_output, binary_cell_11_output, binary_cell_12_output,
       binary_cell_13_output, binary_cell_14_output, binary_cell_15_output, binary_cell_16_output,
       binary_cell_17_output, binary_cell_18_output, binary_cell_19_output, binary_cell_20_output,
       binary_cell_21_output, binary_cell_22_output, binary_cell_23_output, binary_cell_24_output,
       binary_cell_25_output, binary_cell_26_output, binary_cell_27_output, binary_cell_28_output,
       binary_cell_29_output, binary_cell_30_output, binary_cell_31_output, binary_cell_32_output, D0_t,
       D1_t, D2_t, D3_t, D4_t, D5_t, D6_t, D7_t, n2_4_line_decoder_demultiplexer_1_d0,
       n2_4_line_decoder_demultiplexer_1_d1, n2_4_line_decoder_demultiplexer_1_d2,
       n2_4_line_decoder_demultiplexer_1_d3, n2_bit_pipo_mar_1_out0, n2_bit_pipo_mar_1_out1, not_1_out,
       or_2_out, or_4_out, or_5_out, or_6_out, or_8_out, or_9_out, or_11_out, or_13_out, or_14_out;
  wire [7:0] demultiplexer_1_out0, n8_bit_pipo_mbr_1_d0;

  _2_Bit_PIPO_MAR u_2_bit_pipo_mar_1 (
    .Inp0(S0), .Inp1(S1), .Clk(Clk), .Preset(Preset), .En(En), .Clear(Clear), .Out0(n2_bit_pipo_mar_1_out0),
    .Out1(n2_bit_pipo_mar_1_out1), .Load_Control(En));
  _2_4_Line_Decoder_Demultiplexer u_2_4_line_decoder_demultiplexer_1 (
    .S0(n2_bit_pipo_mar_1_out0), .S1(n2_bit_pipo_mar_1_out1), .D0(n2_4_line_decoder_demultiplexer_1_d0),
    .D1(n2_4_line_decoder_demultiplexer_1_d1), .D2(n2_4_line_decoder_demultiplexer_1_d2),
    .D3(n2_4_line_decoder_demultiplexer_1_d3), .En(En));
  Binary_Cell binary_cell_1 (
    .Input(demultiplexer_1_out0[7]), .Output(binary_cell_1_output),
    .Select(n2_4_line_decoder_demultiplexer_1_d0), .Read_Write(nWrite_Read));
  Binary_Cell binary_cell_2 (
    .Input(demultiplexer_1_out0[7]), .Output(binary_cell_2_output),
    .Select(n2_4_line_decoder_demultiplexer_1_d1), .Read_Write(nWrite_Read));
  Binary_Cell binary_cell_3 (
    .Input(demultiplexer_1_out0[7]), .Output(binary_cell_3_output),
    .Select(n2_4_line_decoder_demultiplexer_1_d2), .Read_Write(nWrite_Read));
  Binary_Cell binary_cell_4 (
    .Input(demultiplexer_1_out0[7]), .Output(binary_cell_4_output),
    .Select(n2_4_line_decoder_demultiplexer_1_d3), .Read_Write(nWrite_Read));
  or or_1 (D7_t, binary_cell_4_output, binary_cell_3_output, binary_cell_2_output, binary_cell_1_output);
  not not_1 (not_1_out, nWrite_Read);
  and and_1 (and_1_out, not_1_out, I7);
  or or_2 (or_2_out, and_1_out, and_9_out);
  Binary_Cell binary_cell_5 (
    .Input(demultiplexer_1_out0[6]), .Output(binary_cell_5_output),
    .Select(n2_4_line_decoder_demultiplexer_1_d0), .Read_Write(nWrite_Read));
  Binary_Cell binary_cell_6 (
    .Input(demultiplexer_1_out0[6]), .Output(binary_cell_6_output),
    .Select(n2_4_line_decoder_demultiplexer_1_d1), .Read_Write(nWrite_Read));
  Binary_Cell binary_cell_7 (
    .Input(demultiplexer_1_out0[6]), .Output(binary_cell_7_output),
    .Select(n2_4_line_decoder_demultiplexer_1_d2), .Read_Write(nWrite_Read));
  Binary_Cell binary_cell_8 (
    .Input(demultiplexer_1_out0[6]), .Output(binary_cell_8_output),
    .Select(n2_4_line_decoder_demultiplexer_1_d3), .Read_Write(nWrite_Read));
  or or_3 (D6_t, binary_cell_8_output, binary_cell_7_output, binary_cell_6_output, binary_cell_5_output);
  and and_2 (and_2_out, not_1_out, I5);
  and and_3 (and_3_out, not_1_out, I6);
  or or_4 (or_4_out, and_3_out, and_10_out);
  Binary_Cell binary_cell_9 (
    .Input(demultiplexer_1_out0[5]), .Output(binary_cell_9_output),
    .Select(n2_4_line_decoder_demultiplexer_1_d0), .Read_Write(nWrite_Read));
  Binary_Cell binary_cell_10 (
    .Input(demultiplexer_1_out0[5]), .Output(binary_cell_10_output),
    .Select(n2_4_line_decoder_demultiplexer_1_d1), .Read_Write(nWrite_Read));
  Binary_Cell binary_cell_11 (
    .Input(demultiplexer_1_out0[5]), .Output(binary_cell_11_output),
    .Select(n2_4_line_decoder_demultiplexer_1_d2), .Read_Write(nWrite_Read));
  Binary_Cell binary_cell_12 (
    .Input(demultiplexer_1_out0[5]), .Output(binary_cell_12_output),
    .Select(n2_4_line_decoder_demultiplexer_1_d3), .Read_Write(nWrite_Read));
  and and_4 (and_4_out, not_1_out, I4);
  or or_5 (or_5_out, and_4_out, and_12_out);
  or or_6 (or_6_out, and_2_out, and_11_out);
  or or_7 (D5_t, binary_cell_12_output, binary_cell_11_output, binary_cell_10_output, binary_cell_9_output);
  and and_5 (and_5_out, not_1_out, I2);
  and and_6 (and_6_out, not_1_out, I3);
  or or_8 (or_8_out, and_6_out, and_13_out);
  or or_9 (or_9_out, and_5_out, and_14_out);
  _8_Bit_PIPO_MBR u_8_bit_pipo_mbr_1 (
    .Load_Control(or_14_out), .Clk(Clk), .Preset(Preset), .En(En), .Clear(Clear), .I7(or_2_out),
    .I6(or_4_out), .I5(or_6_out), .I4(or_5_out), .I3(or_8_out), .I2(or_9_out), .I1(or_11_out),
    .I0(or_13_out), .D7(n8_bit_pipo_mbr_1_d0[7]), .D6(n8_bit_pipo_mbr_1_d0[6]), .D5(n8_bit_pipo_mbr_1_d0[5]),
    .D4(n8_bit_pipo_mbr_1_d0[4]), .D3(n8_bit_pipo_mbr_1_d0[3]), .D2(n8_bit_pipo_mbr_1_d0[2]),
    .D1(n8_bit_pipo_mbr_1_d0[1]), .D0(n8_bit_pipo_mbr_1_d0[0]));
  Demultiplexer #(.width(8)) demultiplexer_1 (
    .out0(demultiplexer_1_out0), .out1({D7, D6, D5, D4, D3, D2, D1, D0}), .in(n8_bit_pipo_mbr_1_d0),
    .sel(nWrite_Read), .en(En));
  Binary_Cell binary_cell_13 (
    .Input(demultiplexer_1_out0[4]), .Output(binary_cell_13_output),
    .Select(n2_4_line_decoder_demultiplexer_1_d0), .Read_Write(nWrite_Read));
  Binary_Cell binary_cell_14 (
    .Input(demultiplexer_1_out0[4]), .Output(binary_cell_14_output),
    .Select(n2_4_line_decoder_demultiplexer_1_d1), .Read_Write(nWrite_Read));
  Binary_Cell binary_cell_15 (
    .Input(demultiplexer_1_out0[4]), .Output(binary_cell_15_output),
    .Select(n2_4_line_decoder_demultiplexer_1_d2), .Read_Write(nWrite_Read));
  Binary_Cell binary_cell_16 (
    .Input(demultiplexer_1_out0[4]), .Output(binary_cell_16_output),
    .Select(n2_4_line_decoder_demultiplexer_1_d3), .Read_Write(nWrite_Read));
  or or_10 (D4_t, binary_cell_16_output, binary_cell_15_output, binary_cell_14_output, binary_cell_13_output);
  and and_7 (and_7_out, not_1_out, I1);
  or or_11 (or_11_out, and_7_out, and_15_out);
  Binary_Cell binary_cell_17 (
    .Input(demultiplexer_1_out0[3]), .Output(binary_cell_17_output),
    .Select(n2_4_line_decoder_demultiplexer_1_d0), .Read_Write(nWrite_Read));
  Binary_Cell binary_cell_18 (
    .Input(demultiplexer_1_out0[3]), .Output(binary_cell_18_output),
    .Select(n2_4_line_decoder_demultiplexer_1_d1), .Read_Write(nWrite_Read));
  Binary_Cell binary_cell_19 (
    .Input(demultiplexer_1_out0[3]), .Output(binary_cell_19_output),
    .Select(n2_4_line_decoder_demultiplexer_1_d2), .Read_Write(nWrite_Read));
  Binary_Cell binary_cell_20 (
    .Input(demultiplexer_1_out0[3]), .Output(binary_cell_20_output),
    .Select(n2_4_line_decoder_demultiplexer_1_d3), .Read_Write(nWrite_Read));
  or or_12 (D3_t, binary_cell_20_output, binary_cell_19_output, binary_cell_18_output, binary_cell_17_output);
  and and_8 (and_8_out, not_1_out, I0);
  and and_9 (and_9_out, nWrite_Read, D7_t);
  or or_13 (or_13_out, and_8_out, and_16_out);
  or or_14 (or_14_out, or_13_out, or_11_out, or_9_out, or_8_out, or_5_out, or_6_out, or_4_out, or_2_out);
  Binary_Cell binary_cell_21 (
    .Input(demultiplexer_1_out0[2]), .Output(binary_cell_21_output),
    .Select(n2_4_line_decoder_demultiplexer_1_d0), .Read_Write(nWrite_Read));
  Binary_Cell binary_cell_22 (
    .Input(demultiplexer_1_out0[2]), .Output(binary_cell_22_output),
    .Select(n2_4_line_decoder_demultiplexer_1_d1), .Read_Write(nWrite_Read));
  Binary_Cell binary_cell_23 (
    .Input(demultiplexer_1_out0[2]), .Output(binary_cell_23_output),
    .Select(n2_4_line_decoder_demultiplexer_1_d2), .Read_Write(nWrite_Read));
  Binary_Cell binary_cell_24 (
    .Input(demultiplexer_1_out0[2]), .Output(binary_cell_24_output),
    .Select(n2_4_line_decoder_demultiplexer_1_d3), .Read_Write(nWrite_Read));
  or or_15 (D2_t, binary_cell_24_output, binary_cell_23_output, binary_cell_22_output, binary_cell_21_output);
  and and_10 (and_10_out, nWrite_Read, D6_t);
  Binary_Cell binary_cell_25 (
    .Input(demultiplexer_1_out0[1]), .Output(binary_cell_25_output),
    .Select(n2_4_line_decoder_demultiplexer_1_d0), .Read_Write(nWrite_Read));
  Binary_Cell binary_cell_26 (
    .Input(demultiplexer_1_out0[1]), .Output(binary_cell_26_output),
    .Select(n2_4_line_decoder_demultiplexer_1_d1), .Read_Write(nWrite_Read));
  Binary_Cell binary_cell_27 (
    .Input(demultiplexer_1_out0[1]), .Output(binary_cell_27_output),
    .Select(n2_4_line_decoder_demultiplexer_1_d2), .Read_Write(nWrite_Read));
  Binary_Cell binary_cell_28 (
    .Input(demultiplexer_1_out0[1]), .Output(binary_cell_28_output),
    .Select(n2_4_line_decoder_demultiplexer_1_d3), .Read_Write(nWrite_Read));
  and and_11 (and_11_out, nWrite_Read, D5_t);
  and and_12 (and_12_out, nWrite_Read, D4_t);
  or or_16 (D1_t, binary_cell_28_output, binary_cell_27_output, binary_cell_26_output, binary_cell_25_output);
  and and_13 (and_13_out, nWrite_Read, D3_t);
  Binary_Cell binary_cell_29 (
    .Input(demultiplexer_1_out0[0]), .Output(binary_cell_29_output),
    .Select(n2_4_line_decoder_demultiplexer_1_d0), .Read_Write(nWrite_Read));
  Binary_Cell binary_cell_30 (
    .Input(demultiplexer_1_out0[0]), .Output(binary_cell_30_output),
    .Select(n2_4_line_decoder_demultiplexer_1_d1), .Read_Write(nWrite_Read));
  Binary_Cell binary_cell_31 (
    .Input(demultiplexer_1_out0[0]), .Output(binary_cell_31_output),
    .Select(n2_4_line_decoder_demultiplexer_1_d2), .Read_Write(nWrite_Read));
  Binary_Cell binary_cell_32 (
    .Input(demultiplexer_1_out0[0]), .Output(binary_cell_32_output),
    .Select(n2_4_line_decoder_demultiplexer_1_d3), .Read_Write(nWrite_Read));
  or or_17 (D0_t, binary_cell_32_output, binary_cell_31_output, binary_cell_30_output, binary_cell_29_output);
  and and_14 (and_14_out, nWrite_Read, D2_t);
  and and_15 (and_15_out, nWrite_Read, D1_t);
  and and_16 (and_16_out, nWrite_Read, D0_t);

  // Other names for the same wires on the sheet: Enable = En; nW_R = nWrite_Read

  // Notes on the sheet:
  //   MAR
  //   MBR
endmodule

module _8_Bit_PIPO_MBR (
  input  I7,
  input  I6,
  input  I5,
  input  I4,
  input  I3,
  input  I2,
  input  I1,
  input  I0,
  input  Load_Control,
  input  Clk,
  input  Preset,
  input  En,
  input  Clear,
  output D7,
  output D6,
  output D5,
  output D4,
  output D3,
  output D2,
  output D1,
  output D0
);

  _4_Bit_PIPO_Register_D_FF u_4_bit_pipo_register_d_ff_1 (
    .Inp0(I4), .Inp1(I5), .Inp2(I6), .Inp3(I7), .Out0(D4), .Out1(D5), .Out2(D6), .Out3(D7),
    .Load(Load_Control), .Clk(Clk), .Pr(Preset), .En(En), .Clr(Clear));
  _4_Bit_PIPO_Register_D_FF u_4_bit_pipo_register_d_ff_2 (
    .Inp0(I0), .Inp1(I1), .Inp2(I2), .Inp3(I3), .Out0(D0), .Out1(D1), .Out2(D2), .Out3(D3),
    .Load(Load_Control), .Clk(Clk), .Pr(Preset), .En(En), .Clr(Clear));
endmodule

module _2_Bit_PIPO_MAR (
  input  Load_Control,
  input  Inp0,
  input  Inp1,
  input  Clk,
  input  Preset,
  input  En,
  input  Clear,
  output Out0,
  output Out1
);

  _4_Bit_PIPO_Register_D_FF u_4_bit_pipo_register_d_ff_1 (
    .Inp0(Inp0), .Inp1(Inp1), .Out0(Out0), .Out1(Out1), .Load(Load_Control), .Clk(Clk), .Pr(Preset), .En(En),
    .Clr(Clear));  // open: Inp2, Inp3, Out2, Out3
endmodule
