// Logisim project Regesters.circ as structural Verilog
module _4_Bit_PIPO_Register_D_FF (
  input  Load,
  input  Inp0,
  input  Inp1,
  input  Inp2,
  input  Inp3,
  input  Clk,
  input  Pr,
  input  En,
  input  Clr,
  output Out0,
  output Out1,
  output Out2,
  output Out3
);

  wire and_1_out, and_2_out, and_3_out, and_4_out, and_5_out, and_6_out, and_7_out, and_8_out, not_1_out,
       not_2_out, or_1_out, or_2_out, or_3_out, or_4_out;

  not not_1 (not_1_out, Load);
  not not_2 (not_2_out, not_1_out);
  and and_1 (and_1_out, Out0, not_1_out);
  or or_1 (or_1_out, and_1_out, and_2_out);
  and and_2 (and_2_out, Inp0, not_2_out);
  and and_3 (and_3_out, Out1, not_1_out);
  or or_2 (or_2_out, and_3_out, and_4_out);
  and and_4 (and_4_out, Inp1, not_2_out);
  and and_5 (and_5_out, Out2, not_1_out);
  or or_3 (or_3_out, and_5_out, and_6_out);
  and and_6 (and_6_out, Inp2, not_2_out);
  and and_7 (and_7_out, Out3, not_1_out);
  or or_4 (or_4_out, and_7_out, and_8_out);
  and and_8 (and_8_out, Inp3, not_2_out);
  D_Flip_Flop d_ff_1 (.clk(Clk), .D(or_1_out), .Q(Out0), .preset(Pr), .en(En), .reset(Clr));  // open: Qn
  D_Flip_Flop d_ff_2 (.clk(Clk), .D(or_2_out), .Q(Out1), .preset(Pr), .en(En), .reset(Clr));  // open: Qn
  D_Flip_Flop d_ff_3 (.clk(Clk), .D(or_3_out), .Q(Out2), .preset(Pr), .en(En), .reset(Clr));  // open: Qn
  D_Flip_Flop d_ff_4 (.clk(Clk), .D(or_4_out), .Q(Out3), .preset(Pr), .en(En), .reset(Clr));  // open: Qn
endmodule

module _4_Bit_PIPO_Regester_JK_FF (
  input  Load,
  input  Inp0,
  input  Inp1,
  input  Inp2,
  input  Inp3,
  input  Clk,
  input  Pr,
  input  En,
  input  Clr,
  output Out0,
  output Out1,
  output Out2,
  output Out3
);

  wire and_1_out, and_2_out, and_3_out, and_4_out, and_5_out, and_6_out, and_7_out, and_8_out, buffer_1_out,
       not_1_out, not_2_out, not_3_out, not_4_out;

  not not_1 (not_1_out, Inp0);
  not not_2 (not_2_out, Inp1);
  not not_3 (not_3_out, Inp2);
  not not_4 (not_4_out, Inp3);
  buf buffer_1 (buffer_1_out, Load);
  and and_1 (and_1_out, buffer_1_out, Inp0);
  and and_2 (and_2_out, buffer_1_out, not_1_out);
  and and_3 (and_3_out, buffer_1_out, Inp1);
  and and_4 (and_4_out, buffer_1_out, not_2_out);
  and and_5 (and_5_out, buffer_1_out, Inp2);
  and and_6 (and_6_out, buffer_1_out, not_3_out);
  and and_7 (and_7_out, buffer_1_out, Inp3);
  and and_8 (and_8_out, buffer_1_out, not_4_out);
  J_K_Flip_Flop j_k_ff_1 (
    .J(and_1_out), .clk(Clk), .K(and_2_out), .Q(Out0), .preset(Pr), .en(En), .reset(Clr));  // open: Qn
  J_K_Flip_Flop j_k_ff_2 (
    .J(and_3_out), .clk(Clk), .K(and_4_out), .Q(Out1), .preset(Pr), .en(En), .reset(Clr));  // open: Qn
  J_K_Flip_Flop j_k_ff_3 (
    .J(and_5_out), .clk(Clk), .K(and_6_out), .Q(Out2), .preset(Pr), .en(En), .reset(Clr));  // open: Qn
  J_K_Flip_Flop j_k_ff_4 (
    .J(and_7_out), .clk(Clk), .K(and_8_out), .Q(Out3), .preset(Pr), .en(En), .reset(Clr));  // open: Qn
endmodule

module _4_Bit_SISO_Regester_D_FF (
  input  Inp,
  input  Clk,
  input  Pr,
  input  En,
  input  Clr,
  output Out
);

  wire d_ff_1_q, d_ff_2_q, d_ff_3_q;

  D_Flip_Flop d_ff_1 (.clk(Clk), .D(Inp), .Q(d_ff_1_q), .preset(Pr), .en(En), .reset(Clr));  // open: Qn
  D_Flip_Flop d_ff_2 (.clk(Clk), .D(d_ff_1_q), .Q(d_ff_2_q), .preset(Pr), .en(En), .reset(Clr));  // open: Qn
  D_Flip_Flop d_ff_3 (.clk(Clk), .D(d_ff_2_q), .Q(d_ff_3_q), .preset(Pr), .en(En), .reset(Clr));  // open: Qn
  D_Flip_Flop d_ff_4 (.clk(Clk), .D(d_ff_3_q), .Q(Out), .preset(Pr), .en(En), .reset(Clr));  // open: Qn
endmodule

module _4_Bit_Bidirectional_Shift_Register_With_Parallel_Load (
  input  Clk,
  input  Pr,
  input  En,
  input  Clr,
  input  [1:0] Select_Line,
  input  Right_Shift_Input,
  input  Left_Shift_Input,
  input  Inp3,
  input  Inp2,
  input  Inp1,
  input  Inp0,
  output Out3__Let_SHift_Output,
  output Out2,
  output Out1,
  output Out0__Right_Shift_Output
);

  wire multiplexer_1_out, multiplexer_2_out, multiplexer_3_out, multiplexer_4_out;

  D_Flip_Flop d_ff_1 (
    .clk(Clk), .D(multiplexer_1_out), .Q(Out3__Let_SHift_Output), .preset(Pr), .en(En), .reset(Clr));  // open: Qn
  Multiplexer #(.select(2)) multiplexer_1 (
    .in0(Inp3), .in1(Out2), .in2(Right_Shift_Input), .in3(Out3__Let_SHift_Output), .out(multiplexer_1_out),
    .sel(Select_Line), .en(En));
  Multiplexer #(.select(2)) multiplexer_2 (
    .in0(Inp2), .in1(Out1), .in2(Out3__Let_SHift_Output), .in3(Out2), .out(multiplexer_2_out),
    .sel(Select_Line), .en(En));
  D_Flip_Flop d_ff_2 (.clk(Clk), .D(multiplexer_2_out), .Q(Out2), .preset(Pr), .en(En), .reset(Clr));  // open: Qn
  D_Flip_Flop d_ff_3 (.clk(Clk), .D(multiplexer_3_out), .Q(Out1), .preset(Pr), .en(En), .reset(Clr));  // open: Qn
  Multiplexer #(.select(2)) multiplexer_3 (
    .in0(Inp1), .in1(Out0__Right_Shift_Output), .in2(Out2), .in3(Out1), .out(multiplexer_3_out),
    .sel(Select_Line), .en(En));
  D_Flip_Flop d_ff_4 (
    .clk(Clk), .D(multiplexer_4_out), .Q(Out0__Right_Shift_Output), .preset(Pr), .en(En), .reset(Clr));  // open: Qn
  Multiplexer #(.select(2)) multiplexer_4 (
    .in0(Inp0), .in1(Left_Shift_Input), .in2(Out1), .in3(Out0__Right_Shift_Output), .out(multiplexer_4_out),
    .sel(Select_Line), .en(En));

  // Other names for the same wires on the sheet: s[1:0] = Select_Line
endmodule
